// Logisim project project.circ as structural Verilog: 33 circuits, main circuit proj1_Register_8Bit
module proj1_Register_8Bit (
  input  [7:0] I,
  input  [1:0] FunSel,
  input  E,
  output [7:0] Q
);

  wire and_2_out, and_3_out, and_4_out, and_5_out, and_6_out, and_7_out, and_8_out, and_9_out, and_10_out,
       and_11_out, and_12_out, and_13_out, and_14_out, and_15_out, and_16_out, and_17_out, and_18_out,
       and_19_out, clock_1_out, decoder_1_out0, decoder_1_out1, decoder_1_out2, decoder_1_out3, not_1_out,
       not_2_out, not_3_out, not_4_out, not_5_out, not_6_out, not_7_out, not_8_out, not_9_out, not_10_out,
       not_11_out, or_1_out, or_2_out, or_3_out, or_4_out, or_5_out, or_6_out, or_7_out, or_8_out, or_9_out,
       or_10_out;
  wire [7:0] adder_1_out, multiplexer_1_out;
  wire [7:7] and_1_out;

  Decoder #(.enable("false"), .select(2)) decoder_1 (
    .out0(decoder_1_out0), .out1(decoder_1_out1), .out2(decoder_1_out2), .out3(decoder_1_out3), .sel(FunSel));
  Hex_Digit_Display hex_digit_display_1 (.value(I[7:4]));  // open: dp
  Hex_Digit_Display hex_digit_display_2 (.value(I[3:0]));  // open: dp
  not not_1 (not_1_out, decoder_1_out2);
  and and_1 (and_1_out[7], not_1_out, decoder_1_out3);
  or or_1 (or_1_out, decoder_1_out2, decoder_1_out3);
  Adder adder_1 (.a(Q), .b({{7{and_1_out[7]}}, 1'b1}), .out(adder_1_out));  // open: cin, cout
  not not_2 (not_2_out, decoder_1_out0);
  or or_2 (or_2_out, or_1_out, decoder_1_out0, decoder_1_out1);
  and and_2 (and_2_out, decoder_1_out1, not_3_out);
  not not_3 (not_3_out, or_1_out);
  and and_3 (and_3_out, E, or_2_out);
  Multiplexer #(.width(8)) multiplexer_1 (
    .in0(adder_1_out), .in1(I), .out(multiplexer_1_out), .sel(and_2_out), .en(not_2_out));
  not not_4 (not_4_out, and_3_out);
  not not_5 (not_5_out, and_3_out);
  not not_6 (not_6_out, and_3_out);
  not not_7 (not_7_out, and_3_out);
  not not_8 (not_8_out, and_3_out);
  not not_9 (not_9_out, and_3_out);
  not not_10 (not_10_out, and_3_out);
  not not_11 (not_11_out, and_3_out);
  and and_4 (and_4_out, Q[0], not_4_out);
  and and_5 (and_5_out, and_3_out, multiplexer_1_out[0]);
  and and_6 (and_6_out, Q[1], not_5_out);
  and and_7 (and_7_out, and_3_out, multiplexer_1_out[1]);
  and and_8 (and_8_out, Q[2], not_6_out);
  and and_9 (and_9_out, and_3_out, multiplexer_1_out[2]);
  and and_10 (and_10_out, Q[3], not_7_out);
  and and_11 (and_11_out, and_3_out, multiplexer_1_out[3]);
  and and_12 (and_12_out, Q[4], not_8_out);
  and and_13 (and_13_out, and_3_out, multiplexer_1_out[4]);
  and and_14 (and_14_out, Q[5], not_9_out);
  and and_15 (and_15_out, and_3_out, multiplexer_1_out[5]);
  and and_16 (and_16_out, Q[6], not_10_out);
  and and_17 (and_17_out, and_3_out, multiplexer_1_out[6]);
  and and_18 (and_18_out, Q[7], not_11_out);
  and and_19 (and_19_out, and_3_out, multiplexer_1_out[7]);
  or or_3 (or_3_out, and_4_out, and_5_out);
  or or_4 (or_4_out, and_6_out, and_7_out);
  or or_5 (or_5_out, and_8_out, and_9_out);
  or or_6 (or_6_out, and_10_out, and_11_out);
  or or_7 (or_7_out, and_12_out, and_13_out);
  or or_8 (or_8_out, and_14_out, and_15_out);
  or or_9 (or_9_out, and_16_out, and_17_out);
  or or_10 (or_10_out, and_18_out, and_19_out);
  D_Flip_Flop d_ff_1 (.D(or_3_out), .clk(clock_1_out), .Q(Q[0]));  // open: Qn, preset, reset
  D_Flip_Flop d_ff_2 (.D(or_4_out), .clk(clock_1_out), .Q(Q[1]));  // open: Qn, preset, reset
  D_Flip_Flop d_ff_3 (.D(or_5_out), .clk(clock_1_out), .Q(Q[2]));  // open: Qn, preset, reset
  D_Flip_Flop d_ff_4 (.D(or_6_out), .clk(clock_1_out), .Q(Q[3]));  // open: Qn, preset, reset
  D_Flip_Flop d_ff_5 (.D(or_7_out), .clk(clock_1_out), .Q(Q[4]));  // open: Qn, preset, reset
  D_Flip_Flop d_ff_6 (.D(or_8_out), .clk(clock_1_out), .Q(Q[5]));  // open: Qn, preset, reset
  D_Flip_Flop d_ff_7 (.D(or_9_out), .clk(clock_1_out), .Q(Q[6]));  // open: Qn, preset, reset
  D_Flip_Flop d_ff_8 (.D(or_10_out), .clk(clock_1_out), .Q(Q[7]));  // open: Qn, preset, reset
  Clock clock_1 (.out(clock_1_out));
  Hex_Digit_Display hex_digit_display_3 (.value(Q[7:4]));  // open: dp
  Hex_Digit_Display hex_digit_display_4 (.value(Q[3:0]));  // open: dp
endmodule

module proj1_Register_16Bit (
  input  [15:0] I,
  input  [1:0] FunSel,
  input  E,
  output [15:0] Q
);

  wire and_2_out, and_3_out, and_4_out, and_5_out, and_6_out, and_7_out, and_8_out, and_9_out, and_10_out,
       and_11_out, and_12_out, and_13_out, and_14_out, and_15_out, and_16_out, and_17_out, and_18_out,
       and_19_out, and_20_out, and_21_out, and_22_out, and_23_out, and_24_out, and_25_out, and_26_out,
       and_27_out, and_28_out, and_29_out, and_30_out, and_31_out, and_32_out, and_33_out, and_34_out,
       and_35_out, clock_1_out, decoder_1_out0, decoder_1_out1, decoder_1_out2, decoder_1_out3, not_1_out,
       not_2_out, not_3_out, not_4_out, not_5_out, not_6_out, not_7_out, not_8_out, not_9_out, not_10_out,
       not_11_out, not_12_out, not_13_out, not_14_out, not_15_out, not_16_out, not_17_out, not_18_out,
       not_19_out, or_1_out, or_2_out, or_3_out, or_4_out, or_5_out, or_6_out, or_7_out, or_8_out, or_9_out,
       or_10_out, or_11_out, or_12_out, or_13_out, or_14_out, or_15_out, or_16_out, or_17_out, or_18_out;
  wire [15:0] adder_1_out, multiplexer_1_out;
  wire [15:15] and_1_out;

  Hex_Digit_Display hex_digit_display_1 (.value(I[15:12]));  // open: dp
  Hex_Digit_Display hex_digit_display_2 (.value(I[11:8]));  // open: dp
  Decoder #(.enable("false"), .select(2)) decoder_1 (
    .out0(decoder_1_out0), .out1(decoder_1_out1), .out2(decoder_1_out2), .out3(decoder_1_out3), .sel(FunSel));
  Hex_Digit_Display hex_digit_display_3 (.value(I[7:4]));  // open: dp
  Hex_Digit_Display hex_digit_display_4 (.value(I[3:0]));  // open: dp
  not not_1 (not_1_out, decoder_1_out2);
  and and_1 (and_1_out[15], not_1_out, decoder_1_out3);
  or or_1 (or_1_out, decoder_1_out2, decoder_1_out3);
  Adder #(.width(16)) adder_1 (.a(Q), .b({{15{and_1_out[15]}}, 1'b1}), .out(adder_1_out));  // open: cin, cout
  not not_2 (not_2_out, decoder_1_out0);
  or or_2 (or_2_out, or_1_out, decoder_1_out0, decoder_1_out1);
  Multiplexer #(.width(16)) multiplexer_1 (
    .in0(adder_1_out), .in1(I), .out(multiplexer_1_out), .sel(and_2_out), .en(not_2_out));
  and and_2 (and_2_out, decoder_1_out1, not_3_out);
  not not_3 (not_3_out, or_1_out);
  and and_3 (and_3_out, E, or_2_out);
  not not_4 (not_4_out, and_3_out);
  not not_5 (not_5_out, and_3_out);
  not not_6 (not_6_out, and_3_out);
  not not_7 (not_7_out, and_3_out);
  not not_8 (not_8_out, and_3_out);
  not not_9 (not_9_out, and_3_out);
  not not_10 (not_10_out, and_3_out);
  not not_11 (not_11_out, and_3_out);
  not not_12 (not_12_out, and_3_out);
  not not_13 (not_13_out, and_3_out);
  not not_14 (not_14_out, and_3_out);
  not not_15 (not_15_out, and_3_out);
  not not_16 (not_16_out, and_3_out);
  not not_17 (not_17_out, and_3_out);
  not not_18 (not_18_out, and_3_out);
  not not_19 (not_19_out, and_3_out);
  and and_4 (and_4_out, Q[0], not_4_out);
  and and_5 (and_5_out, and_3_out, multiplexer_1_out[0]);
  and and_6 (and_6_out, Q[1], not_5_out);
  and and_7 (and_7_out, and_3_out, multiplexer_1_out[1]);
  and and_8 (and_8_out, Q[2], not_6_out);
  and and_9 (and_9_out, and_3_out, multiplexer_1_out[2]);
  and and_10 (and_10_out, Q[3], not_7_out);
  and and_11 (and_11_out, and_3_out, multiplexer_1_out[3]);
  and and_12 (and_12_out, Q[4], not_8_out);
  and and_13 (and_13_out, and_3_out, multiplexer_1_out[4]);
  and and_14 (and_14_out, Q[5], not_9_out);
  and and_15 (and_15_out, and_3_out, multiplexer_1_out[5]);
  and and_16 (and_16_out, Q[6], not_10_out);
  and and_17 (and_17_out, and_3_out, multiplexer_1_out[6]);
  and and_18 (and_18_out, Q[7], not_11_out);
  and and_19 (and_19_out, and_3_out, multiplexer_1_out[7]);
  and and_20 (and_20_out, Q[8], not_12_out);
  and and_21 (and_21_out, and_3_out, multiplexer_1_out[8]);
  and and_22 (and_22_out, Q[9], not_13_out);
  and and_23 (and_23_out, and_3_out, multiplexer_1_out[9]);
  and and_24 (and_24_out, Q[10], not_14_out);
  and and_25 (and_25_out, and_3_out, multiplexer_1_out[10]);
  and and_26 (and_26_out, Q[11], not_15_out);
  and and_27 (and_27_out, and_3_out, multiplexer_1_out[11]);
  and and_28 (and_28_out, Q[12], not_16_out);
  and and_29 (and_29_out, and_3_out, multiplexer_1_out[12]);
  and and_30 (and_30_out, Q[13], not_17_out);
  and and_31 (and_31_out, and_3_out, multiplexer_1_out[13]);
  and and_32 (and_32_out, Q[14], not_18_out);
  and and_33 (and_33_out, and_3_out, multiplexer_1_out[14]);
  and and_34 (and_34_out, Q[15], not_19_out);
  and and_35 (and_35_out, and_3_out, multiplexer_1_out[15]);
  or or_3 (or_3_out, and_4_out, and_5_out);
  or or_4 (or_4_out, and_6_out, and_7_out);
  or or_5 (or_5_out, and_8_out, and_9_out);
  or or_6 (or_6_out, and_10_out, and_11_out);
  or or_7 (or_7_out, and_12_out, and_13_out);
  or or_8 (or_8_out, and_14_out, and_15_out);
  or or_9 (or_9_out, and_16_out, and_17_out);
  or or_10 (or_10_out, and_18_out, and_19_out);
  or or_11 (or_11_out, and_20_out, and_21_out);
  or or_12 (or_12_out, and_22_out, and_23_out);
  or or_13 (or_13_out, and_24_out, and_25_out);
  or or_14 (or_14_out, and_26_out, and_27_out);
  or or_15 (or_15_out, and_28_out, and_29_out);
  or or_16 (or_16_out, and_30_out, and_31_out);
  or or_17 (or_17_out, and_32_out, and_33_out);
  or or_18 (or_18_out, and_34_out, and_35_out);
  D_Flip_Flop d_ff_1 (.D(or_3_out), .clk(clock_1_out), .Q(Q[0]));  // open: Qn, preset, reset
  D_Flip_Flop d_ff_2 (.D(or_4_out), .clk(clock_1_out), .Q(Q[1]));  // open: Qn, preset, reset
  D_Flip_Flop d_ff_3 (.D(or_5_out), .clk(clock_1_out), .Q(Q[2]));  // open: Qn, preset, reset
  D_Flip_Flop d_ff_4 (.D(or_6_out), .clk(clock_1_out), .Q(Q[3]));  // open: Qn, preset, reset
  D_Flip_Flop d_ff_5 (.D(or_7_out), .clk(clock_1_out), .Q(Q[4]));  // open: Qn, preset, reset
  D_Flip_Flop d_ff_6 (.D(or_8_out), .clk(clock_1_out), .Q(Q[5]));  // open: Qn, preset, reset
  D_Flip_Flop d_ff_7 (.D(or_9_out), .clk(clock_1_out), .Q(Q[6]));  // open: Qn, preset, reset
  D_Flip_Flop d_ff_8 (.D(or_10_out), .clk(clock_1_out), .Q(Q[7]));  // open: Qn, preset, reset
  D_Flip_Flop d_ff_9 (.D(or_11_out), .clk(clock_1_out), .Q(Q[8]));  // open: Qn, preset, reset
  D_Flip_Flop d_ff_10 (.D(or_12_out), .clk(clock_1_out), .Q(Q[9]));  // open: Qn, preset, reset
  D_Flip_Flop d_ff_11 (.D(or_13_out), .clk(clock_1_out), .Q(Q[10]));  // open: Qn, preset, reset
  D_Flip_Flop d_ff_12 (.D(or_14_out), .clk(clock_1_out), .Q(Q[11]));  // open: Qn, preset, reset
  D_Flip_Flop d_ff_13 (.D(or_15_out), .clk(clock_1_out), .Q(Q[12]));  // open: Qn, preset, reset
  D_Flip_Flop d_ff_14 (.D(or_16_out), .clk(clock_1_out), .Q(Q[13]));  // open: Qn, preset, reset
  D_Flip_Flop d_ff_15 (.D(or_17_out), .clk(clock_1_out), .Q(Q[14]));  // open: Qn, preset, reset
  D_Flip_Flop d_ff_16 (.D(or_18_out), .clk(clock_1_out), .Q(Q[15]));  // open: Qn, preset, reset
  Clock clock_1 (.out(clock_1_out));
  Hex_Digit_Display hex_digit_display_5 (.value(Q[15:12]));  // open: dp
  Hex_Digit_Display hex_digit_display_6 (.value(Q[11:8]));  // open: dp
  Hex_Digit_Display hex_digit_display_7 (.value(Q[7:4]));  // open: dp
  Hex_Digit_Display hex_digit_display_8 (.value(Q[3:0]));  // open: dp
endmodule

module proj1_RegFile_2a (
  input  [7:0] I,
  input  [3:0] RegSel,
  input  [1:0] FunSel,
  input  [1:0] OutASel,
  input  [1:0] OutBSel,
  output [7:0] OutA,
  output [7:0] OutB
);

  wire [7:0] R0_q, R1_q, R2_q, R3_q;

  Hex_Digit_Display hex_digit_display_1 (.value(I[7:4]));  // open: dp
  Hex_Digit_Display hex_digit_display_2 (.value(I[3:0]));  // open: dp
  proj1_Register_8Bit R3 (.Q(R3_q), .FunSel(FunSel), .I(I), .E(RegSel[3]));
  proj1_Register_8Bit R2 (.Q(R2_q), .FunSel(FunSel), .I(I), .E(RegSel[2]));
  proj1_Register_8Bit R1 (.Q(R1_q), .FunSel(FunSel), .I(I), .E(RegSel[1]));
  proj1_Register_8Bit R0 (.Q(R0_q), .FunSel(FunSel), .I(I), .E(RegSel[0]));
  Multiplexer #(.enable("false"), .select(2), .width(8)) multiplexer_1 (
    .in0(R0_q), .in1(R1_q), .in2(R2_q), .in3(R3_q), .out(OutA), .sel(OutASel));
  Multiplexer #(.enable("false"), .select(2), .width(8)) multiplexer_2 (
    .in0(R0_q), .in1(R1_q), .in2(R2_q), .in3(R3_q), .out(OutB), .sel(OutBSel));
  Hex_Digit_Display hex_digit_display_3 (.value(OutA[7:4]));  // open: dp
  Hex_Digit_Display hex_digit_display_4 (.value(OutB[7:4]));  // open: dp
  Hex_Digit_Display hex_digit_display_5 (.value(OutA[3:0]));  // open: dp
  Hex_Digit_Display hex_digit_display_6 (.value(OutB[3:0]));  // open: dp
endmodule

module proj1_RegFile_2b (
  input  [7:0] I,
  input  [2:0] RegSel,
  input  [1:0] FunSel,
  input  [1:0] OutCSel,
  input  [1:0] OutDSel,
  output [7:0] OutC,
  output [7:0] OutD
);

  wire [7:0] AR_q, PC_q, SP_q;

  Hex_Digit_Display hex_digit_display_1 (.value(I[7:4]));  // open: dp
  Hex_Digit_Display hex_digit_display_2 (.value(I[3:0]));  // open: dp
  proj1_Register_8Bit SP (.Q(SP_q), .FunSel(FunSel), .I(I), .E(RegSel[2]));
  proj1_Register_8Bit AR (.Q(AR_q), .FunSel(FunSel), .I(I), .E(RegSel[1]));
  proj1_Register_8Bit PC (.Q(PC_q), .FunSel(FunSel), .I(I), .E(RegSel[0]));
  Multiplexer #(.enable("false"), .select(2), .width(8)) multiplexer_1 (
    .in0(PC_q), .in1(AR_q), .in2(SP_q), .in3(PC_q), .out(OutC), .sel(OutCSel));
  Multiplexer #(.enable("false"), .select(2), .width(8)) multiplexer_2 (
    .in0(PC_q), .in1(AR_q), .in2(SP_q), .in3(PC_q), .out(OutD), .sel(OutDSel));
  Hex_Digit_Display hex_digit_display_3 (.value(OutC[7:4]));  // open: dp
  Hex_Digit_Display hex_digit_display_4 (.value(OutD[7:4]));  // open: dp
  Hex_Digit_Display hex_digit_display_5 (.value(OutC[3:0]));  // open: dp
  Hex_Digit_Display hex_digit_display_6 (.value(OutD[3:0]));  // open: dp
endmodule

module proj1_IR (
  input  [7:0] I,
  input  H,
  input  Enable,
  input  [1:0] FunSel,
  output [15:0] IRout
);

  wire and_1_out, and_2_out, and_3_out, isDec_out, isEmpty_out, isFull_out, isInc_out, nor_1_out, not_1_out,
       not_2_out, not_3_out, not_4_out;
  wire [1:0] multiplexer_3_out, multiplexer_4_out, multiplexer_5_out, multiplexer_6_out;
  wire [1:1] or_1_out;
  wire [7:0] multiplexer_1_out, multiplexer_2_out;

  Hex_Digit_Display hex_digit_display_1 (.value(I[7:4]));  // open: dp
  Hex_Digit_Display hex_digit_display_2 (.value(I[3:0]));  // open: dp
  not not_1 (not_1_out, FunSel[1]);
  not not_2 (not_2_out, FunSel[0]);
  and and_1 (and_1_out, H, nor_1_out);
  and and_2 (and_2_out, not_1_out, FunSel[0]);
  and and_3 (and_3_out, FunSel[1], not_2_out);
  or or_1 (or_1_out[1], and_2_out, and_3_out);
  Multiplexer #(.enable("false"), .width(8)) multiplexer_1 (
    .in0(IRout[15:8]), .in1(I), .out(multiplexer_1_out), .sel(and_1_out));
  proj1_Register_8Bit IR_H (.Q(IRout[15:8]), .FunSel(multiplexer_3_out), .I(multiplexer_1_out), .E(Enable));
  not not_3 (not_3_out, FunSel[1]);
  and isInc (isInc_out, not_3_out, or_1_out[1]);
  and isDec (isDec_out, FunSel[1], or_1_out[1]);
  Multiplexer #(.enable("false"), .width(8)) multiplexer_2 (
    .in0(I), .in1(IRout[7:0]), .out(multiplexer_2_out), .sel(and_1_out));
  proj1_Register_8Bit IR_L (.Q(IRout[7:0]), .FunSel({or_1_out[1], FunSel[1]}), .I(multiplexer_2_out), .E(Enable));
  not not_4 (not_4_out, isDec_out);
  Hex_Digit_Display hex_digit_display_3 (.value(IRout[15:12]));  // open: dp
  and isFull (isFull_out, IRout[0], IRout[1], IRout[2], IRout[3], IRout[4], IRout[5], IRout[6], IRout[7], isInc_out);
  nor isEmpty (isEmpty_out, IRout[0], IRout[1], IRout[2], IRout[3], IRout[4], IRout[5], IRout[6], IRout[7], not_4_out);
  nor nor_1 (nor_1_out, isInc_out, isDec_out);
  Hex_Digit_Display hex_digit_display_4 (.value(IRout[11:8]));  // open: dp
  Hex_Digit_Display hex_digit_display_5 (.value(IRout[7:4]));  // open: dp
  Multiplexer #(.enable("false"), .width(2)) multiplexer_3 (
    .in0(multiplexer_6_out), .in1({or_1_out[1], FunSel[1]}), .out(multiplexer_3_out), .sel(nor_1_out));
  Hex_Digit_Display hex_digit_display_6 (.value(IRout[3:0]));  // open: dp
  Multiplexer #(.disabled("Z"), .enable("false"), .width(2)) multiplexer_4 (
    .in0(2'b01), .in1(2'b10), .out(multiplexer_4_out), .sel(isFull_out));
  Multiplexer #(.disabled("Z"), .enable("false"), .width(2)) multiplexer_5 (
    .in0(2'b01), .in1(2'b11), .out(multiplexer_5_out), .sel(isEmpty_out));
  Multiplexer #(.enable("false"), .width(2)) multiplexer_6 (
    .in0(multiplexer_4_out), .in1(multiplexer_5_out), .out(multiplexer_6_out), .sel(isEmpty_out));

  // Notes on the sheet:
  //   Fatih Uzunoğlu. 08/03/2020
endmodule

module proj1_IR2_ver2 (
  input  H,
  input  [7:0] I,
  input  Enable,
  input  [1:0] FunSel,
  output [7:0] IR_L,
  output [7:0] IR_H
);

  wire and_1_out, and_2_out, not_1_out, not_2_out;
  wire [1:1] or_1_out;
  wire [15:0] multiplexer_1_out;

  Hex_Digit_Display hex_digit_display_1 (.value(I[7:4]));  // open: dp
  Hex_Digit_Display hex_digit_display_2 (.value(I[3:0]));  // open: dp
  not not_1 (not_1_out, FunSel[1]);
  not not_2 (not_2_out, FunSel[0]);
  and and_1 (and_1_out, not_1_out, FunSel[0]);
  and and_2 (and_2_out, FunSel[1], not_2_out);
  or or_1 (or_1_out[1], and_1_out, and_2_out);
  Multiplexer #(.enable("false"), .width(16)) multiplexer_1 (
    .in0({IR_H, I}), .in1({I, IR_L}), .out(multiplexer_1_out), .sel(H));
  proj1_Register_16Bit IR (.Q({IR_H, IR_L}), .FunSel({or_1_out[1], FunSel[1]}), .I(multiplexer_1_out), .E(Enable));
  Hex_Digit_Display hex_digit_display_3 (.value(IR_H[7:4]));  // open: dp
  Hex_Digit_Display hex_digit_display_4 (.value(IR_L[7:4]));  // open: dp
  Hex_Digit_Display hex_digit_display_5 (.value(IR_H[3:0]));  // open: dp
  Hex_Digit_Display hex_digit_display_6 (.value(IR_L[3:0]));  // open: dp
endmodule

module proj2_flagRegister (
  input  [3:0] in_1,
  output O,
  output N,
  output C,
  output Z
);

  wire clock_1_out;

  D_Flip_Flop d_ff_1 (.D(in_1[0]), .clk(clock_1_out), .Q(O));  // open: Qn, preset, reset
  D_Flip_Flop d_ff_2 (.D(in_1[1]), .clk(clock_1_out), .Q(N));  // open: Qn, preset, reset
  D_Flip_Flop d_ff_3 (.D(in_1[2]), .clk(clock_1_out), .Q(C));  // open: Qn, preset, reset
  D_Flip_Flop d_ff_4 (.D(in_1[3]), .clk(clock_1_out), .Q(Z));  // open: Qn, preset, reset
  Clock clock_1 (.out(clock_1_out));
  LED OLed (.in(O));
  LED NLed (.in(N));
  LED CLed (.in(C));
  LED ZLed (.in(Z));
endmodule

module proj2_ALU_arithmeticUnit (
  input  Carry,
  input  [1:0] mode,
  input  [7:0] A,
  input  [7:0] B,
  output Z,
  output [7:0] aOut,
  output C,
  output O,
  output N
);

  wire adder_1_cout, and_1_out, and_2_out, and_3_out, and_4_out, and_5_out, borrowToCarry_out,
       decoder_1_out1, decoder_1_out2, not_1_out, not_2_out, not_3_out, not_4_out, not_5_out, not_6_out,
       or_1_out, or_2_out, subtractor_1_bout;
  wire [7:0] adder_1_out, subtractor_1_out;

  Decoder #(.enable("false"), .select(2)) decoder_1 (
    .out1(decoder_1_out1), .out2(decoder_1_out2), .sel(mode));  // open: out0, out3
  and and_1 (and_1_out, Carry, decoder_1_out1);
  Adder adder_1 (.a(A), .b(B), .out(adder_1_out), .cin(and_1_out), .cout(adder_1_cout));
  Subtractor subtractor_1 (.a(A), .b(B), .out(subtractor_1_out), .bout(subtractor_1_bout));  // open: bin
  not not_1 (not_1_out, A[7]);
  not not_2 (not_2_out, B[7]);
  not not_3 (not_3_out, aOut[7]);
  not not_4 (not_4_out, A[7]);
  not not_5 (not_5_out, B[7]);
  not not_6 (not_6_out, aOut[7]);
  and and_2 (and_2_out, not_1_out, not_2_out, aOut[7]);
  and and_3 (and_3_out, A[7], B[7], not_3_out);
  and and_4 (and_4_out, not_4_out, B[7], aOut[7]);
  and and_5 (and_5_out, A[7], not_5_out, not_6_out);
  Multiplexer #(.enable("false"), .width(8)) multiplexer_1 (
    .in0(adder_1_out), .in1(subtractor_1_out), .out(aOut), .sel(decoder_1_out2));
  Multiplexer #(.enable("false")) multiplexer_2 (
    .in0(adder_1_cout), .in1(borrowToCarry_out), .out(C), .sel(decoder_1_out2));
  not borrowToCarry (borrowToCarry_out, subtractor_1_bout);
  or or_1 (or_1_out, and_2_out, and_3_out);
  or or_2 (or_2_out, and_4_out, and_5_out);
  Multiplexer #(.enable("false")) multiplexer_3 (.in0(or_1_out), .in1(or_2_out), .out(O), .sel(decoder_1_out2));
  nor nor_1 (Z, aOut[0], aOut[1], aOut[2], aOut[3], aOut[4], aOut[5], aOut[6], aOut[7]);

  assign N = aOut[7];
endmodule

module proj2_ALU_shiftUnit (
  input  [7:0] inputVar,
  input  [2:0] mode,
  input  Carry,
  output C,
  output [7:0] sOut,
  output Z,
  output N,
  output O
);

  wire xor_1_out, xor_2_out, xor_3_out;

  Multiplexer #(.enable("false"), .select(3)) multiplexer_1 (
    .in0(inputVar[7]), .in1(inputVar[0]), .in4(inputVar[7]), .in5(inputVar[0]), .out(C), .sel(mode));  // open: in2, in3, in6, in7
  xor xor_1 (xor_1_out, inputVar[7], inputVar[6]);
  xor xor_2 (xor_2_out, inputVar[6], inputVar[7]);
  xor xor_3 (xor_3_out, inputVar[7], Carry);
  Multiplexer #(.enable("false"), .select(3), .width(8)) multiplexer_2 (
    .in0({inputVar[6:0], 1'b0}), .in1({1'b0, inputVar[7:1]}), .in2({inputVar[6:0], 1'b0}),
    .in3({{2{inputVar[7]}}, inputVar[6:1]}), .in4({inputVar[6:0], Carry}), .in5({Carry, inputVar[7:1]}),
    .out({N, sOut[6:0]}), .sel(mode));  // open: in6, in7
  Multiplexer #(.enable("false"), .select(3)) multiplexer_3 (
    .in2(xor_1_out), .in4(xor_2_out), .in5(xor_3_out), .out(O), .sel(mode));  // open: in0, in1, in3, in6, in7
  nor nor_1 (Z, sOut[0], sOut[1], sOut[2], sOut[3], sOut[4], sOut[5], sOut[6], N);

  assign sOut[7] = N;
endmodule

module proj2_ALU_logicUnit (
  input  [7:0] A,
  input  [7:0] B,
  input  [2:0] mode,
  output Z,
  output N,
  output [7:0] lOut
);

  wire [7:0] and_1_out, not_1_out, not_2_out, or_1_out, xor_1_out;

  assign not_1_out = ~A;  // NOT_Gate not_1, 8 bits wide
  assign not_2_out = ~B;  // NOT_Gate not_2, 8 bits wide
  Multiplexer #(.enable("false"), .select(3), .width(8)) multiplexer_1 (
    .in0(A), .in1(B), .in2(not_1_out), .in3(not_2_out), .in4(and_1_out), .in5(or_1_out), .in6(xor_1_out),
    .out(lOut), .sel(mode));  // open: in7
  assign and_1_out = A & B;  // AND_Gate and_1, 8 bits wide
  assign or_1_out = A | B;  // OR_Gate or_1, 8 bits wide
  nor nor_1 (Z, lOut[0], lOut[1], lOut[2], lOut[3], lOut[4], lOut[5], lOut[6], lOut[7]);
  assign xor_1_out = A ^ B;  // XOR_Gate xor_1, 8 bits wide

  assign N = lOut[7];
endmodule

module proj2_ALU_implementation (
  input  [7:0] A,
  input  Cin,
  input  [7:0] B,
  input  [3:0] FunSel,
  output [3:0] Flags_ZCNO,
  output [7:0] OutAlu
);

  wire and_1_out, and_2_out, and_3_out, and_4_out, and_6_out, and_7_out, and_8_out, and_9_out, not_1_out,
       not_2_out, not_3_out, proj2_alu_arithmeticunit_1_c, proj2_alu_arithmeticunit_1_n,
       proj2_alu_arithmeticunit_1_o, proj2_alu_arithmeticunit_1_z, proj2_alu_logicunit_1_n,
       proj2_alu_logicunit_1_z, proj2_alu_shiftunit_1_c, proj2_alu_shiftunit_1_n, proj2_alu_shiftunit_1_o,
       proj2_alu_shiftunit_1_z;
  wire [1:0] or_5_out;
  wire [2:0] or_3_out;
  wire [2:1] not_4_out;
  wire [7:0] proj2_alu_arithmeticunit_1_aout, proj2_alu_logicunit_1_lout, proj2_alu_shiftunit_1_sout;

  or or_1 (or_3_out[2], FunSel[3], FunSel[2]);
  and and_1 (and_1_out, FunSel[0], FunSel[3]);
  or or_2 (or_3_out[1], and_1_out, and_2_out);
  not not_1 (not_1_out, FunSel[3]);
  and and_2 (and_2_out, FunSel[1], not_2_out);
  and and_3 (and_3_out, not_1_out, not_2_out, FunSel[0]);
  not not_2 (not_2_out, FunSel[2]);
  not not_3 (not_3_out, FunSel[0]);
  and and_4 (and_4_out, FunSel[3], not_3_out);
  or or_3 (or_3_out[0], and_3_out, and_4_out);
  and and_5 (not_4_out[2], FunSel[2], FunSel[1]);
  not not_4 (not_4_out[1], FunSel[1]);
  proj2_ALU_logicUnit proj2_alu_logicunit_1 (
    .lOut(proj2_alu_logicunit_1_lout), .Z(proj2_alu_logicunit_1_z), .N(proj2_alu_logicunit_1_n),
    .mode(or_3_out), .A(A), .B(B));
  and and_6 (and_6_out, FunSel[2], FunSel[3]);
  and and_7 (and_7_out, FunSel[1], FunSel[3]);
  and and_8 (and_8_out, ~FunSel[3], FunSel[2], ~FunSel[1]);  // AND_Gate
  and and_9 (and_9_out, ~FunSel[3], FunSel[2], ~FunSel[0]);  // AND_Gate
  proj2_ALU_shiftUnit proj2_alu_shiftunit_1 (
    .C(proj2_alu_shiftunit_1_c), .O(proj2_alu_shiftunit_1_o), .sOut(proj2_alu_shiftunit_1_sout),
    .N(proj2_alu_shiftunit_1_n), .Z(proj2_alu_shiftunit_1_z), .inputVar(A), .Carry(Cin),
    .mode({not_4_out, FunSel[0]}));
  or or_4 (or_5_out[1], and_6_out, and_7_out);
  or or_5 (or_5_out[0], and_8_out, and_9_out);
  proj2_ALU_arithmeticUnit proj2_alu_arithmeticunit_1 (
    .N(proj2_alu_arithmeticunit_1_n), .aOut(proj2_alu_arithmeticunit_1_aout),
    .C(proj2_alu_arithmeticunit_1_c), .O(proj2_alu_arithmeticunit_1_o), .Z(proj2_alu_arithmeticunit_1_z),
    .A(A), .B(B), .mode(FunSel[1:0]), .Carry(Cin));
  Multiplexer #(.disabled("Z"), .enable("false"), .select(2), .width(8)) multiplexer_1 (
    .in0(proj2_alu_logicunit_1_lout), .in1(proj2_alu_arithmeticunit_1_aout),
    .in2(proj2_alu_shiftunit_1_sout), .out(OutAlu), .sel(or_5_out));  // open: in3
  Multiplexer #(.disabled("Z"), .enable("false"), .select(2)) multiplexer_2 (
    .in0(proj2_alu_logicunit_1_z), .in1(proj2_alu_arithmeticunit_1_z), .in2(proj2_alu_shiftunit_1_z),
    .out(Flags_ZCNO[3]), .sel(or_5_out));  // open: in3
  Multiplexer #(.disabled("Z"), .enable("false"), .select(2)) multiplexer_3 (
    .in1(proj2_alu_arithmeticunit_1_c), .in2(proj2_alu_shiftunit_1_c), .out(Flags_ZCNO[2]), .sel(or_5_out));  // open: in0, in3
  Multiplexer #(.disabled("Z"), .enable("false"), .select(2)) multiplexer_4 (
    .in1(proj2_alu_arithmeticunit_1_o), .in2(proj2_alu_shiftunit_1_o), .out(Flags_ZCNO[0]), .sel(or_5_out));  // open: in0, in3
  Multiplexer #(.disabled("Z"), .enable("false"), .select(2)) multiplexer_5 (
    .in0(proj2_alu_logicunit_1_n), .in1(proj2_alu_arithmeticunit_1_n), .in2(proj2_alu_shiftunit_1_n),
    .out(Flags_ZCNO[1]), .sel(or_5_out));  // open: in3
endmodule

module proj2_ALU_testbed (
  input  [7:0] in_1,
  input  [7:0] in_2,
  input  [3:0] FunSel,
  output [7:0] out_4
);

  wire proj2_flagregister_1_c;
  wire [3:0] proj2_alu_implementation_1_flags_zcno;

  Hex_Digit_Display hex_digit_display_1 (.value(in_1[7:4]));  // open: dp
  Hex_Digit_Display hex_digit_display_2 (.value(in_2[7:4]));  // open: dp
  Hex_Digit_Display hex_digit_display_3 (.value(in_1[3:0]));  // open: dp
  Hex_Digit_Display hex_digit_display_4 (.value(in_2[3:0]));  // open: dp
  proj2_ALU_implementation proj2_alu_implementation_1 (
    .OutAlu(out_4), .Flags_ZCNO(proj2_alu_implementation_1_flags_zcno), .FunSel(FunSel), .A(in_2), .B(in_1),
    .Cin(proj2_flagregister_1_c));
  Hex_Digit_Display hex_digit_display_5 (.value(out_4[7:4]));  // open: dp
  proj2_flagRegister proj2_flagregister_1 (
    .C(proj2_flagregister_1_c), .in_1(proj2_alu_implementation_1_flags_zcno));  // open: O, N, Z
  Hex_Digit_Display hex_digit_display_6 (.value(out_4[3:0]));  // open: dp
endmodule

module proj3_Organization (
);

  wire clock_1_out, proj2_flagregister_1_c, proj2_flagregister_1_z, proj3_controlunit_1_ir_enable,
       proj3_controlunit_1_ir_selh, proj3_controlunit_1_muxcsel, proj3_controlunit_1_ram_writeenable;
  wire [1:0] proj3_controlunit_1_ar_funsel, proj3_controlunit_1_gpr_funsel, proj3_controlunit_1_ir_funsel,
       proj3_controlunit_1_muxasel, proj3_controlunit_1_muxbsel, proj3_controlunit_1_outasel,
       proj3_controlunit_1_outbsel, proj3_controlunit_1_outcsel, proj3_controlunit_1_outdsel;
  wire [2:0] proj3_controlunit_1_ar_regsel;
  wire [3:0] proj2_alu_implementation_1_flags_zcno, proj3_controlunit_1_alu_funsel,
       proj3_controlunit_1_gpr_regsel;
  wire [7:0] multiplexer_1_out, multiplexer_2_out, multiplexer_3_out, proj1_ir2_ver2_1_ir_h,
       proj1_ir2_ver2_1_ir_l, proj1_regfile_2a_1_outa, proj1_regfile_2a_1_outb, proj1_regfile_2b_1_outc,
       proj1_regfile_2b_1_outd, proj2_alu_implementation_1_outalu, ram_1_dout;

  Multiplexer #(.enable("false"), .select(2), .width(8)) multiplexer_1 (
    .in0(proj1_ir2_ver2_1_ir_l), .in1(ram_1_dout), .in2(proj1_regfile_2b_1_outc),
    .in3(proj2_alu_implementation_1_outalu), .out(multiplexer_1_out), .sel(proj3_controlunit_1_muxasel));
  proj1_IR2_ver2 proj1_ir2_ver2_1 (
    .IR_L(proj1_ir2_ver2_1_ir_l), .IR_H(proj1_ir2_ver2_1_ir_h), .FunSel(proj3_controlunit_1_ir_funsel),
    .I(ram_1_dout), .H(proj3_controlunit_1_ir_selh), .Enable(proj3_controlunit_1_ir_enable));
  proj1_RegFile_2a proj1_regfile_2a_1 (
    .OutA(proj1_regfile_2a_1_outa), .OutB(proj1_regfile_2a_1_outb), .I(multiplexer_1_out),
    .RegSel(proj3_controlunit_1_gpr_regsel), .FunSel(proj3_controlunit_1_gpr_funsel),
    .OutASel(proj3_controlunit_1_outasel), .OutBSel(proj3_controlunit_1_outbsel));
  Multiplexer #(.enable("false"), .select(2), .width(8)) multiplexer_2 (
    .in1(proj1_ir2_ver2_1_ir_l), .in2(ram_1_dout), .in3(proj2_alu_implementation_1_outalu),
    .out(multiplexer_2_out), .sel(proj3_controlunit_1_muxbsel));  // open: in0
  Multiplexer #(.enable("false"), .width(8)) multiplexer_3 (
    .in0(multiplexer_1_out), .in1(proj1_regfile_2a_1_outa), .out(multiplexer_3_out),
    .sel(proj3_controlunit_1_muxcsel));
  proj2_ALU_implementation proj2_alu_implementation_1 (
    .OutAlu(proj2_alu_implementation_1_outalu), .Flags_ZCNO(proj2_alu_implementation_1_flags_zcno),
    .FunSel(proj3_controlunit_1_alu_funsel), .A(multiplexer_3_out), .B(proj1_regfile_2a_1_outb),
    .Cin(proj2_flagregister_1_c));
  proj2_flagRegister proj2_flagregister_1 (
    .C(proj2_flagregister_1_c), .Z(proj2_flagregister_1_z), .in_1(proj2_alu_implementation_1_flags_zcno));  // open: O, N
  proj1_RegFile_2b proj1_regfile_2b_1 (
    .OutC(proj1_regfile_2b_1_outc), .OutD(proj1_regfile_2b_1_outd), .I(multiplexer_2_out),
    .RegSel(proj3_controlunit_1_ar_regsel), .FunSel(proj3_controlunit_1_ar_funsel),
    .OutCSel(proj3_controlunit_1_outcsel), .OutDSel(proj3_controlunit_1_outdsel));
  Clock clock_1 (.out(clock_1_out));
  RAM #(.asyncread("true"), .\type ("nonvolatile")) ram_1 (
    .addr(proj1_regfile_2b_1_outd), .we(proj3_controlunit_1_ram_writeenable), .oe(1'b1), .clk(clock_1_out),
    .din(proj2_alu_implementation_1_outalu), .dout(ram_1_dout));
  proj3_controlUnit proj3_controlunit_1 (
    .AR_RegSel(proj3_controlunit_1_ar_regsel), .OutCSel(proj3_controlunit_1_outcsel),
    .MuxBSel(proj3_controlunit_1_muxbsel), .AR_FunSel(proj3_controlunit_1_ar_funsel),
    .OutDSel(proj3_controlunit_1_outdsel), .IR_selH(proj3_controlunit_1_ir_selh),
    .IR_FunSel(proj3_controlunit_1_ir_funsel), .IR_Enable(proj3_controlunit_1_ir_enable),
    .MuxCSel(proj3_controlunit_1_muxcsel), .MuxASel(proj3_controlunit_1_muxasel),
    .OutASel(proj3_controlunit_1_outasel), .OutBSel(proj3_controlunit_1_outbsel),
    .GPR_RegSel(proj3_controlunit_1_gpr_regsel), .GPR_FunSel(proj3_controlunit_1_gpr_funsel),
    .ALU_FunSel(proj3_controlunit_1_alu_funsel), .RAM_WriteEnable(proj3_controlunit_1_ram_writeenable),
    .IR_L(proj1_ir2_ver2_1_ir_l), .IR_H(proj1_ir2_ver2_1_ir_h), .Z(proj2_flagregister_1_z));
endmodule

module proj3_sequenceCounter (
  input  RESET,
  input  CLOCK,
  output [7:0] cOUT
);

  wire [2:0] counter_1_q;

  Counter #(.max('h7), .width(3)) counter_1 (
    .clr(RESET), .load(1'b0), .up(1'b1), .count(1'b1), .clk(CLOCK), .Q(counter_1_q));  // open: D, carry
  Hex_Digit_Display hex_digit_display_1 (.value({1'b0, counter_1_q}));  // open: dp
  Decoder #(.enable("false"), .select(3)) decoder_1 (
    .out0(cOUT[0]), .out1(cOUT[1]), .out2(cOUT[2]), .out3(cOUT[3]), .out4(cOUT[4]), .out5(cOUT[5]),
    .out6(cOUT[6]), .out7(cOUT[7]), .sel(counter_1_q));
endmodule

module proj3_controlUnit (
  input  [7:0] IR_H,
  input  [7:0] IR_L,
  input  Z,
  output [2:0] AR_RegSel,
  output [1:0] OutCSel,
  output [1:0] MuxBSel,
  output [1:0] AR_FunSel,
  output [1:0] OutDSel,
  output IR_selH,
  output [1:0] IR_FunSel,
  output IR_Enable,
  output MuxCSel,
  output [1:0] MuxASel,
  output [1:0] OutASel,
  output [1:0] OutBSel,
  output [3:0] GPR_RegSel,
  output [1:0] GPR_FunSel,
  output [3:0] ALU_FunSel,
  output RAM_WriteEnable
);

  wire clock_1_out, decoder_1_out0, decoder_1_out1, decoder_1_out2, decoder_1_out3, decoder_1_out4,
       decoder_1_out5, decoder_1_out6, decoder_1_out7, decoder_1_out8, decoder_1_out9, decoder_1_out10,
       decoder_1_out11, decoder_1_out12, decoder_1_out13, decoder_1_out14, decoder_1_out15, decoder_1_out16,
       decoder_1_out17, decoder_1_out18, or_1_out, or_2_out, proj3_controlunit_ld_1_counterreset;
  wire [7:0] proj3_sequencecounter_1_cout;

  Hex_Digit_Display hex_digit_display_1 (.value(IR_H[7:4]));  // open: dp
  Hex_Digit_Display hex_digit_display_2 (.value(IR_H[3:0]));  // open: dp
  Hex_Digit_Display hex_digit_display_3 (.value(IR_L[7:4]), .dp(IR_L[4]));
  Clock clock_1 (.out(clock_1_out));
  Hex_Digit_Display hex_digit_display_4 (.value(IR_L[3:0]));  // open: dp
  Decoder #(.enable("false"), .select(5)) decoder_1 (
    .out0(decoder_1_out0), .out1(decoder_1_out1), .out2(decoder_1_out2), .out3(decoder_1_out3),
    .out4(decoder_1_out4), .out5(decoder_1_out5), .out6(decoder_1_out6), .out7(decoder_1_out7),
    .out8(decoder_1_out8), .out9(decoder_1_out9), .out10(decoder_1_out10), .out11(decoder_1_out11),
    .out12(decoder_1_out12), .out13(decoder_1_out13), .out14(decoder_1_out14), .out15(decoder_1_out15),
    .out16(decoder_1_out16), .out17(decoder_1_out17), .out18(decoder_1_out18), .sel(IR_H[7:3]));  // open: out19, out20, out21, out22, out23, out24, out25, out26, out27, out28, out29, out30, out31
  or or_1 (or_1_out, decoder_1_out13, decoder_1_out12, decoder_1_out11, decoder_1_out10, decoder_1_out9, decoder_1_out6, decoder_1_out5);
  or or_2 (or_2_out, decoder_1_out8, decoder_1_out7);
  proj3_sequenceCounter proj3_sequencecounter_1 (
    .cOUT(proj3_sequencecounter_1_cout), .RESET(proj3_controlunit_ld_1_counterreset), .CLOCK(clock_1_out));
  proj3_controlUnit_fetch proj3_controlunit_fetch_1 (
    .ARegSel(AR_RegSel), .AFunSel(AR_FunSel), .OutDSel(OutDSel), .IR_selH(IR_selH), .IR_FunSel(IR_FunSel),
    .IR_Enable(IR_Enable), .Counter(proj3_sequencecounter_1_cout));
  proj3_controlUnit_LD proj3_controlunit_ld_1 (
    .RegSel(GPR_RegSel), .FunSel(GPR_FunSel), .MuxASel(MuxASel), .OutDSel(OutDSel),
    .CounterReset(proj3_controlunit_ld_1_counterreset), .isEnabled(decoder_1_out0),
    .Counter(proj3_sequencecounter_1_cout), .IR_H(IR_H));
  proj3_controlUnit_ST proj3_controlunit_st_1 (
    .CounterReset(proj3_controlunit_ld_1_counterreset), .FunSelAlu(ALU_FunSel), .OutDSel(OutDSel),
    .RAM_WriteEnable(RAM_WriteEnable), .OutASel(OutASel), .MuxCSel(MuxCSel), .isEnabled(decoder_1_out1),
    .Counter(proj3_sequencecounter_1_cout), .IR_H(IR_H));
  proj3_controlUnit_MOV proj3_controlunit_mov_1 (
    .FunSel(GPR_FunSel), .RegSel(GPR_RegSel), .OutCSel(OutCSel), .MuxASel(MuxASel), .FunSelAlu(ALU_FunSel),
    .MuxBSel(MuxBSel), .ARegSel(AR_RegSel), .AFunSel(AR_FunSel), .OutBSel(OutBSel), .MuxCSel(MuxCSel),
    .CounterReset(proj3_controlunit_ld_1_counterreset), .IR_L(IR_L), .isEnabled(decoder_1_out2),
    .Counter(proj3_sequencecounter_1_cout), .IR_H(IR_H));
  proj3_controlUnit_PSH proj3_controlunit_psh_1 (
    .CounterReset(proj3_controlunit_ld_1_counterreset), .FunSelAlu(ALU_FunSel), .ARegSel(AR_RegSel),
    .RAM_WriteEnable(RAM_WriteEnable), .AFunSel(AR_FunSel), .OutBSel(OutBSel), .OutDSel(OutDSel),
    .isEnabled(decoder_1_out3), .Counter(proj3_sequencecounter_1_cout), .IR_L(IR_L));
  proj3_controlUnit_PUL proj3_controlunit_pul_1 (
    .RegSel(GPR_RegSel), .FunSel(GPR_FunSel), .MuxASel(MuxASel), .FunSelAlu(ALU_FunSel), .ARegSel(AR_RegSel),
    .AFunSel(AR_FunSel), .OutDSel(OutDSel), .CounterReset(proj3_controlunit_ld_1_counterreset),
    .isEnabled(decoder_1_out4), .Counter(proj3_sequencecounter_1_cout), .IR_L(IR_L));
  proj3_controlUnit_ALUOperations proj3_controlunit_aluoperations_1 (
    .RegSel(GPR_RegSel), .FunSel(GPR_FunSel), .OutCSel(OutCSel), .MuxASel(MuxASel), .FunSelAlu(ALU_FunSel),
    .MuxBSel(MuxBSel), .ARegSel(AR_RegSel), .AFunSel(AR_FunSel), .OutASel(OutASel), .OutBSel(OutBSel),
    .MuxCSel(MuxCSel), .CounterReset(proj3_controlunit_ld_1_counterreset), .IR_L(IR_L), .isEnabled(or_1_out),
    .Counter(proj3_sequencecounter_1_cout), .IR_H(IR_H));
  proj3_controlUnit_INCDEC proj3_controlunit_incdec_1 (
    .CounterReset(proj3_controlunit_ld_1_counterreset), .FunSelAlu(ALU_FunSel), .OutCSel(OutCSel),
    .MuxCSel(MuxCSel), .MuxASel(MuxASel), .MuxBSel(MuxBSel), .OutBSel(OutBSel), .RegSel(GPR_RegSel),
    .FunSel(GPR_FunSel), .ARegSel(AR_RegSel), .AFunSel(AR_FunSel), .IR_H(IR_H), .IR_L(IR_L),
    .isEnabled(or_2_out), .Counter(proj3_sequencecounter_1_cout));
  proj3_controlUnit_BRA proj3_controlunit_bra_1 (
    .ARegSel(AR_RegSel), .MuxBSel(MuxBSel), .AFunSel(AR_FunSel), .IR_selH(IR_selH),
    .CounterReset(proj3_controlunit_ld_1_counterreset), .isEnabled(decoder_1_out14),
    .Counter(proj3_sequencecounter_1_cout));
  proj3_controlUnit_BEQ proj3_controlunit_beq_1 (
    .CounterReset(proj3_controlunit_ld_1_counterreset), .MuxBSel(MuxBSel), .ARegSel(AR_RegSel),
    .AFunSel(AR_FunSel), .IR_selH(IR_selH), .isEnabled(decoder_1_out15),
    .Counter(proj3_sequencecounter_1_cout), .Z(Z));
  proj3_controlUnit_BNE proj3_controlunit_bne_1 (
    .CounterReset(proj3_controlunit_ld_1_counterreset), .MuxBSel(MuxBSel), .ARegSel(AR_RegSel),
    .AFunSel(AR_FunSel), .IR_selH(IR_selH), .isEnabled(decoder_1_out16),
    .Counter(proj3_sequencecounter_1_cout), .Z(Z));
  proj3_controlUnit_CALL proj3_controlunit_call_1 (
    .IR_selH(IR_selH), .OutDSel(OutDSel), .OutCSel(OutCSel), .MuxASel(MuxASel), .FunSelAlu(ALU_FunSel),
    .MuxBSel(MuxBSel), .ARegSel(AR_RegSel), .AFunSel(AR_FunSel), .MuxCSel(MuxCSel),
    .RAM_WriteEnable(RAM_WriteEnable), .CounterReset(proj3_controlunit_ld_1_counterreset),
    .isEnabled(decoder_1_out17), .Counter(proj3_sequencecounter_1_cout));
  proj3_controlUnit_RET proj3_controlunit_ret_1 (
    .CounterReset(proj3_controlunit_ld_1_counterreset), .OutDSel(OutDSel), .MuxBSel(MuxBSel),
    .ARegSel(AR_RegSel), .AFunSel(AR_FunSel), .isEnabled(decoder_1_out18),
    .Counter(proj3_sequencecounter_1_cout));
  // Pins of 1 and 4 bits meet at IR_L[7:4]

  // Other names for the same wires on the sheet: AFunSel[1:0] = AR_FunSel; ARegSel[2:0] = AR_RegSel;
  //   FunSel[1:0] = GPR_FunSel; FunSelAlu[3:0] = ALU_FunSel; RegSel[3:0] = GPR_RegSel
endmodule

module proj3_controlUnit_fetch (
  input  [7:0] Counter,
  output [2:0] ARegSel,
  output [1:0] AFunSel,
  output [1:0] OutDSel,
  output IR_selH,
  output [1:0] IR_FunSel,
  output IR_Enable
);

  assign OutDSel = Counter[0] ? 2'b00 : 2'bz;  // Controlled_Buffer controlled_buffer_1
  assign ARegSel = Counter[1] ? 3'b001 : 3'bz;  // Controlled_Buffer controlled_buffer_2
  assign IR_Enable = Counter[0] ? 1'b1 : 1'bz;  // Controlled_Buffer controlled_buffer_3
  assign AFunSel = Counter[1] ? 2'b10 : 2'bz;  // Controlled_Buffer controlled_buffer_4
  assign IR_FunSel = Counter[0] ? 2'b11 : 2'bz;  // Controlled_Buffer controlled_buffer_5
  assign IR_selH = Counter[1] ? 1'b0 : 1'bz;  // Controlled_Buffer controlled_buffer_6
  assign OutDSel = Counter[1] ? 2'b00 : 2'bz;  // Controlled_Buffer controlled_buffer_7
  assign ARegSel = Counter[0] ? 3'b001 : 3'bz;  // Controlled_Buffer controlled_buffer_8
  assign AFunSel = Counter[0] ? 2'b10 : 2'bz;  // Controlled_Buffer controlled_buffer_9
  assign IR_Enable = Counter[1] ? 1'b1 : 1'bz;  // Controlled_Buffer controlled_buffer_10
  assign IR_selH = Counter[0] ? 1'b1 : 1'bz;  // Controlled_Buffer controlled_buffer_11
  assign IR_FunSel = Counter[1] ? 2'b11 : 2'bz;  // Controlled_Buffer controlled_buffer_12
endmodule

module proj3_controlUnit_ALUOperations (
  input  [7:0] Counter,
  input  isEnabled,
  input  [7:0] IR_H,
  input  [7:0] IR_L,
  output CounterReset,
  output [3:0] RegSel,
  output [1:0] FunSel,
  output [1:0] OutCSel,
  output [1:0] MuxASel,
  output [3:0] FunSelAlu,
  output [1:0] MuxBSel,
  output [2:0] ARegSel,
  output [1:0] AFunSel,
  output [1:0] OutASel,
  output [1:0] OutBSel,
  output MuxCSel
);

  wire and_2_out, and_3_out, and_4_out, and_5_out, and_6_out, and_7_out, and_12_out, decoder_1_out4,
       decoder_1_out5, decoder_2_out4, decoder_2_out5, decoder_3_out4, decoder_3_out5, dstreg_AR, dstreg_PC,
       dstreg_R0, dstreg_R1, dstreg_R2, dstreg_R3, dstreg_SP, or_1_out, or_4_out, or_6_out, or_7_out,
       srcreg1_AR, srcreg1_PC, srcreg1_R0, srcreg1_R1, srcreg1_R2, srcreg1_R3, srcreg1_SP, srcreg2_AR,
       srcreg2_PC, srcreg2_R0, srcreg2_R1, srcreg2_R2, srcreg2_R3, srcreg2_SP;
  wire [1:0] and_9_out, and_11_out;
  wire [2:0] mode;
  wire [3:0] multiplexer_1_out;
  wire [7:0] and_1_out, bit_extender_1_out;

  assign bit_extender_1_out = {{7{isEnabled}}, isEnabled};  // Bit_Extender bit_extender_1
  or or_1 (or_1_out, srcreg1_PC, srcreg1_AR, srcreg1_SP);
  assign and_1_out = Counter & bit_extender_1_out;  // AND_Gate and_1, 8 bits wide
  and and_2 (and_2_out, or_1_out, and_1_out[2]);
  assign MuxASel = and_2_out ? 2'b10 : 2'bz;  // Controlled_Buffer controlled_buffer_1
  assign CounterReset = and_1_out[3] ? 1'b1 : 1'bz;  // Controlled_Buffer controlled_buffer_2
  and and_3 (and_3_out, IR_H[6], IR_H[5]);
  or or_2 (mode[2], and_3_out, and_5_out);
  Multiplexer #(.enable("false"), .select(3), .width(4)) multiplexer_1 (
    .in0(4'b0100), .in1(4'b0110), .in2(4'b0111), .in3(4'b1000), .in4(4'b0010), .in5(4'b1010), .in6(4'b1011),
    .out(multiplexer_1_out), .sel(mode));  // open: in7
  and and_4 (and_4_out, IR_H[6], ~IR_H[4], IR_H[3]);  // AND_Gate
  and and_5 (and_5_out, IR_H[4], IR_H[3]);
  not not_1 (mode[0], IR_H[3]);
  assign OutCSel = and_1_out[2] ? {srcreg1_SP, srcreg1_AR} : 2'bz;  // Controlled_Buffer controlled_buffer_3
  assign FunSelAlu = and_1_out[2] ? multiplexer_1_out : 4'bz;  // Controlled_Buffer controlled_buffer_4
  and and_6 (and_6_out, ~IR_H[5], ~IR_H[3]);  // AND_Gate
  or or_3 (mode[1], and_4_out, and_6_out);
  Decoder #(.enable("false"), .select(3)) decoder_1 (
    .out0(dstreg_R0), .out1(dstreg_R1), .out2(dstreg_R2), .out3(dstreg_R3), .out4(decoder_1_out4),
    .out5(decoder_1_out5), .out6(dstreg_AR), .out7(dstreg_SP), .sel(IR_H[2:0]));
  and and_7 (and_7_out, or_4_out, and_1_out[2]);
  or or_4 (or_4_out, dstreg_PC, dstreg_AR, dstreg_SP);
  or or_5 (dstreg_PC, decoder_1_out4, decoder_1_out5);
  or or_6 (or_6_out, srcreg1_R0, srcreg1_R2, srcreg1_R1, srcreg1_R0);
  and and_8 (and_9_out[1], ~srcreg1_R0, ~srcreg1_R1);  // AND_Gate
  and and_9 (and_9_out[0], ~srcreg1_R2, ~srcreg1_R0);  // AND_Gate
  assign MuxBSel = and_7_out ? 2'b11 : 2'bz;  // Controlled_Buffer controlled_buffer_5
  assign OutASel = and_1_out[2] ? and_9_out : 2'bz;  // Controlled_Buffer controlled_buffer_6
  assign ARegSel = and_7_out ? {dstreg_SP, dstreg_AR, dstreg_PC} : 3'bz;  // Controlled_Buffer controlled_buffer_7
  assign AFunSel = and_7_out ? 2'b01 : 2'bz;  // Controlled_Buffer controlled_buffer_8
  Decoder #(.enable("false"), .select(3)) decoder_2 (
    .out0(srcreg1_R0), .out1(srcreg1_R1), .out2(srcreg1_R2), .out3(srcreg1_R3), .out4(decoder_2_out4),
    .out5(decoder_2_out5), .out6(srcreg1_AR), .out7(srcreg1_SP), .sel(IR_L[7:5]));
  and and_10 (and_11_out[1], ~srcreg2_R0, ~srcreg2_R1);  // AND_Gate
  and and_11 (and_11_out[0], ~srcreg2_R2, ~srcreg2_R0);  // AND_Gate
  or or_7 (or_7_out, dstreg_R0, dstreg_R1, dstreg_R3, dstreg_R2);
  assign MuxASel = and_12_out ? 2'b11 : 2'bz;  // Controlled_Buffer controlled_buffer_9
  and and_12 (and_12_out, and_1_out[2], or_7_out);
  or or_8 (srcreg1_PC, decoder_2_out4, decoder_2_out5);
  assign OutBSel = and_1_out[2] ? and_11_out : 2'bz;  // Controlled_Buffer controlled_buffer_10
  assign RegSel = and_12_out ? {dstreg_R3, dstreg_R2, dstreg_R1, dstreg_R0} : 4'bz;  // Controlled_Buffer controlled_buffer_11
  Decoder #(.enable("false"), .select(3)) decoder_3 (
    .out0(srcreg2_R0), .out1(srcreg2_R1), .out2(srcreg2_R2), .out3(srcreg2_R3), .out4(decoder_3_out4),
    .out5(decoder_3_out5), .out6(srcreg2_AR), .out7(srcreg2_SP), .sel(IR_L[4:2]));
  assign MuxCSel = and_1_out[2] ? or_6_out : 1'bz;  // Controlled_Buffer controlled_buffer_12
  or or_9 (srcreg2_PC, decoder_3_out4, decoder_3_out5);
  assign FunSel = and_12_out ? 2'b01 : 2'bz;  // Controlled_Buffer controlled_buffer_13
endmodule

module proj3_controlUnit_LD (
  input  [7:0] Counter,
  input  isEnabled,
  input  [7:0] IR_H,
  output CounterReset,
  output [3:0] RegSel,
  output [1:0] FunSel,
  output [1:0] MuxASel,
  output [1:0] OutDSel
);

  wire and_2_out, and_3_out, regsel_R0, regsel_R1, regsel_R2, regsel_R3;
  wire [7:0] and_1_out, bit_extender_1_out;

  assign bit_extender_1_out = {{7{isEnabled}}, isEnabled};  // Bit_Extender bit_extender_1
  assign and_1_out = Counter & bit_extender_1_out;  // AND_Gate and_1, 8 bits wide
  and and_2 (and_2_out, IR_H[0], and_1_out[2]);
  assign OutDSel = and_2_out ? 2'b01 : 2'bz;  // Controlled_Buffer controlled_buffer_1
  assign CounterReset = and_1_out[3] ? 1'b1 : 1'bz;  // Controlled_Buffer controlled_buffer_2
  assign MuxASel = and_2_out ? 2'b01 : 2'bz;  // Controlled_Buffer controlled_buffer_3
  Decoder #(.enable("false"), .select(2)) decoder_1 (
    .out0(regsel_R0), .out1(regsel_R1), .out2(regsel_R2), .out3(regsel_R3), .sel(IR_H[2:1]));
  and and_3 (and_3_out, ~IR_H[0], and_1_out[2]);  // AND_Gate
  assign MuxASel = and_3_out ? 2'b00 : 2'bz;  // Controlled_Buffer controlled_buffer_4
  assign FunSel = and_1_out[2] ? 2'b01 : 2'bz;  // Controlled_Buffer controlled_buffer_5
  assign RegSel = and_1_out[2] ? {regsel_R3, regsel_R2, regsel_R1, regsel_R0} : 4'bz;  // Controlled_Buffer controlled_buffer_6

  // Other names for the same wires on the sheet: isDirect = IR_H[0]
endmodule

module proj3_controlUnit_ST (
  input  [7:0] Counter,
  input  isEnabled,
  input  [7:0] IR_H,
  output [3:0] FunSelAlu,
  output CounterReset,
  output [1:0] OutASel,
  output MuxCSel,
  output [1:0] OutDSel,
  output RAM_WriteEnable
);

  wire regsel_R0, regsel_R1, regsel_R2, regsel_R3;
  wire [1:0] and_2_out;
  wire [7:0] and_3_out, bit_extender_1_out;

  assign bit_extender_1_out = {{7{isEnabled}}, isEnabled};  // Bit_Extender bit_extender_1
  and and_1 (and_2_out[1], ~regsel_R0, ~regsel_R1);  // AND_Gate
  and and_2 (and_2_out[0], ~regsel_R2, ~regsel_R0);  // AND_Gate
  assign and_3_out = Counter & bit_extender_1_out;  // AND_Gate and_3, 8 bits wide
  assign OutASel = and_3_out[2] ? and_2_out : 2'bz;  // Controlled_Buffer controlled_buffer_1
  assign MuxCSel = and_3_out[2] ? 1'b1 : 1'bz;  // Controlled_Buffer controlled_buffer_2
  Decoder #(.enable("false"), .select(2)) decoder_1 (
    .out0(regsel_R0), .out1(regsel_R1), .out2(regsel_R2), .out3(regsel_R3), .sel(IR_H[2:1]));
  assign FunSelAlu = and_3_out[2] ? 4'b0000 : 4'bz;  // Controlled_Buffer controlled_buffer_3
  assign CounterReset = and_3_out[3] ? 1'b1 : 1'bz;  // Controlled_Buffer controlled_buffer_4
  assign RAM_WriteEnable = and_3_out[2] ? 1'b1 : 1'bz;  // Controlled_Buffer controlled_buffer_5
  assign OutDSel = and_3_out[2] ? 2'b01 : 2'bz;  // Controlled_Buffer controlled_buffer_6
endmodule

module proj3_controlUnit_MOV (
  input  [7:0] Counter,
  input  isEnabled,
  input  [7:0] IR_H,
  input  [7:0] IR_L,
  output CounterReset,
  output [3:0] RegSel,
  output [1:0] FunSel,
  output [1:0] OutCSel,
  output [1:0] MuxASel,
  output [3:0] FunSelAlu,
  output [1:0] MuxBSel,
  output [2:0] ARegSel,
  output [1:0] AFunSel,
  output MuxCSel,
  output [1:0] OutBSel
);

  wire and_2_out, and_3_out, and_6_out, and_7_out, and_8_out, and_9_out, decoder_1_out4, decoder_1_out5,
       decoder_2_out4, decoder_2_out5, dstreg_AR, dstreg_PC, dstreg_R0, dstreg_R1, dstreg_R2, dstreg_R3,
       dstreg_SP, or_1_out, or_2_out, or_4_out, or_5_out, or_7_out, or_8_out, or_9_out, or_10_out,
       srcreg1_AR, srcreg1_PC, srcreg1_R0, srcreg1_R1, srcreg1_R2, srcreg1_R3, srcreg1_SP;
  wire [1:0] and_5_out;
  wire [7:0] and_1_out, bit_extender_1_out;

  assign bit_extender_1_out = {{7{isEnabled}}, isEnabled};  // Bit_Extender bit_extender_1
  assign and_1_out = Counter & bit_extender_1_out;  // AND_Gate and_1, 8 bits wide
  or or_1 (or_1_out, srcreg1_PC, srcreg1_AR, srcreg1_SP);
  and and_2 (and_2_out, or_1_out, and_1_out[2], or_2_out);
  or or_2 (or_2_out, dstreg_R3, dstreg_R2, dstreg_R1, dstreg_R0);
  assign RegSel = and_2_out ? {dstreg_R3, dstreg_R2, dstreg_R1, dstreg_R0} : 4'bz;  // Controlled_Buffer controlled_buffer_1
  assign CounterReset = and_1_out[3] ? 1'b1 : 1'bz;  // Controlled_Buffer controlled_buffer_2
  assign FunSel = and_2_out ? 2'b01 : 2'bz;  // Controlled_Buffer controlled_buffer_3
  Decoder #(.enable("false"), .select(3)) decoder_1 (
    .out0(dstreg_R0), .out1(dstreg_R1), .out2(dstreg_R2), .out3(dstreg_R3), .out4(decoder_1_out4),
    .out5(decoder_1_out5), .out6(dstreg_AR), .out7(dstreg_SP), .sel(IR_H[2:0]));
  assign OutCSel = and_2_out ? {srcreg1_SP, srcreg1_AR} : 2'bz;  // Controlled_Buffer controlled_buffer_4
  or or_3 (dstreg_PC, decoder_1_out4, decoder_1_out5);
  assign MuxASel = and_2_out ? 2'b10 : 2'bz;  // Controlled_Buffer controlled_buffer_5
  or or_4 (or_4_out, srcreg1_R0, srcreg1_R1, srcreg1_R2, srcreg1_R3);
  or or_5 (or_5_out, dstreg_SP, dstreg_AR, dstreg_PC);
  Decoder #(.enable("false"), .select(3)) decoder_2 (
    .out0(srcreg1_R0), .out1(srcreg1_R1), .out2(srcreg1_R2), .out3(srcreg1_R3), .out4(decoder_2_out4),
    .out5(decoder_2_out5), .out6(srcreg1_AR), .out7(srcreg1_SP), .sel(IR_L[7:5]));
  assign ARegSel = and_3_out ? {dstreg_SP, dstreg_AR, dstreg_PC} : 3'bz;  // Controlled_Buffer controlled_buffer_6
  and and_3 (and_3_out, or_4_out, and_1_out[2], or_5_out);
  or or_6 (srcreg1_PC, decoder_2_out4, decoder_2_out5);
  and and_4 (and_5_out[1], ~srcreg1_R0, ~srcreg1_R1);  // AND_Gate
  and and_5 (and_5_out[0], ~srcreg1_R2, ~srcreg1_R0);  // AND_Gate
  assign AFunSel = and_3_out ? 2'b01 : 2'bz;  // Controlled_Buffer controlled_buffer_7
  assign OutBSel = and_3_out ? and_5_out : 2'bz;  // Controlled_Buffer controlled_buffer_8
  or or_7 (or_7_out, srcreg1_PC, srcreg1_AR, srcreg1_SP);
  or or_8 (or_8_out, srcreg1_R0, srcreg1_R1, srcreg1_R2, srcreg1_R3);
  and and_6 (and_6_out, and_7_out, or_9_out);
  and and_7 (and_7_out, or_7_out, and_1_out[2]);
  or or_9 (or_9_out, dstreg_SP, dstreg_AR, dstreg_PC);
  assign MuxBSel = and_3_out ? 2'b11 : 2'bz;  // Controlled_Buffer controlled_buffer_9
  and and_8 (and_8_out, or_8_out, and_1_out[2]);
  or or_10 (or_10_out, dstreg_R3, dstreg_R2, dstreg_R1, dstreg_R0);
  assign ARegSel = and_6_out ? {dstreg_SP, dstreg_AR, dstreg_PC} : 3'bz;  // Controlled_Buffer controlled_buffer_10
  assign RegSel = and_9_out ? {dstreg_R3, dstreg_R2, dstreg_R1, dstreg_R0} : 4'bz;  // Controlled_Buffer controlled_buffer_11
  and and_9 (and_9_out, and_8_out, or_10_out);
  assign FunSelAlu = and_3_out ? 4'b0001 : 4'bz;  // Controlled_Buffer controlled_buffer_12
  assign AFunSel = and_6_out ? 2'b01 : 2'bz;  // Controlled_Buffer controlled_buffer_13
  assign FunSel = and_9_out ? 2'b01 : 2'bz;  // Controlled_Buffer controlled_buffer_14
  assign OutCSel = and_6_out ? {srcreg1_SP, srcreg1_AR} : 2'bz;  // Controlled_Buffer controlled_buffer_15
  assign MuxASel = and_9_out ? 2'b11 : 2'bz;  // Controlled_Buffer controlled_buffer_16
  assign MuxCSel = and_6_out ? 1'b0 : 1'bz;  // Controlled_Buffer controlled_buffer_17
  assign FunSelAlu = and_9_out ? 4'b0001 : 4'bz;  // Controlled_Buffer controlled_buffer_18
  assign MuxASel = and_6_out ? 2'b10 : 2'bz;  // Controlled_Buffer controlled_buffer_19
  assign OutBSel = and_9_out ? and_5_out : 2'bz;  // Controlled_Buffer controlled_buffer_20
  assign FunSelAlu = and_6_out ? 4'b0000 : 4'bz;  // Controlled_Buffer controlled_buffer_21
  assign MuxBSel = and_6_out ? 2'b11 : 2'bz;  // Controlled_Buffer controlled_buffer_22
endmodule

module proj3_controlUnit_PSH (
  input  [7:0] Counter,
  input  isEnabled,
  input  [7:0] IR_L,
  output CounterReset,
  output [3:0] FunSelAlu,
  output [2:0] ARegSel,
  output [1:0] AFunSel,
  output RAM_WriteEnable,
  output [1:0] OutBSel,
  output [1:0] OutDSel
);

  wire regsel_R0, regsel_R1, regsel_R2, regsel_R3;
  wire [1:0] and_3_out;
  wire [7:0] and_1_out, bit_extender_1_out;

  assign bit_extender_1_out = {{7{isEnabled}}, isEnabled};  // Bit_Extender bit_extender_1
  assign and_1_out = Counter & bit_extender_1_out;  // AND_Gate and_1, 8 bits wide
  and and_2 (and_3_out[1], ~regsel_R0, ~regsel_R1);  // AND_Gate
  and and_3 (and_3_out[0], ~regsel_R2, ~regsel_R0);  // AND_Gate
  assign OutBSel = and_1_out[2] ? and_3_out : 2'bz;  // Controlled_Buffer controlled_buffer_1
  assign ARegSel = and_1_out[3] ? 3'b100 : 3'bz;  // Controlled_Buffer controlled_buffer_2
  assign FunSelAlu = and_1_out[2] ? 4'b0001 : 4'bz;  // Controlled_Buffer controlled_buffer_3
  assign AFunSel = and_1_out[3] ? 2'b11 : 2'bz;  // Controlled_Buffer controlled_buffer_4
  Decoder #(.enable("false"), .select(2)) decoder_1 (
    .out0(regsel_R0), .out1(regsel_R1), .out2(regsel_R2), .out3(regsel_R3), .sel(IR_L[2:1]));
  assign CounterReset = and_1_out[4] ? 1'b1 : 1'bz;  // Controlled_Buffer controlled_buffer_5
  assign OutDSel = and_1_out[2] ? 2'b10 : 2'bz;  // Controlled_Buffer controlled_buffer_6
  assign RAM_WriteEnable = and_1_out[2] ? 1'b1 : 1'bz;  // Controlled_Buffer controlled_buffer_7
endmodule

module proj3_controlUnit_PUL (
  input  [7:0] Counter,
  input  isEnabled,
  input  [7:0] IR_L,
  output CounterReset,
  output [3:0] FunSelAlu,
  output [2:0] ARegSel,
  output [1:0] AFunSel,
  output [3:0] RegSel,
  output [1:0] FunSel,
  output [1:0] OutDSel,
  output [1:0] MuxASel
);

  wire regsel_R0, regsel_R1, regsel_R2, regsel_R3;
  wire [7:0] and_1_out, bit_extender_1_out;

  assign bit_extender_1_out = {{7{isEnabled}}, isEnabled};  // Bit_Extender bit_extender_1
  assign and_1_out = Counter & bit_extender_1_out;  // AND_Gate and_1, 8 bits wide
  assign ARegSel = and_1_out[2] ? 3'b100 : 3'bz;  // Controlled_Buffer controlled_buffer_1
  assign OutDSel = and_1_out[3] ? 2'b10 : 2'bz;  // Controlled_Buffer controlled_buffer_2
  assign CounterReset = and_1_out[4] ? 1'b1 : 1'bz;  // Controlled_Buffer controlled_buffer_3
  assign AFunSel = and_1_out[2] ? 2'b10 : 2'bz;  // Controlled_Buffer controlled_buffer_4
  assign MuxASel = and_1_out[3] ? 2'b01 : 2'bz;  // Controlled_Buffer controlled_buffer_5
  Decoder #(.enable("false"), .select(2)) decoder_1 (
    .out0(regsel_R0), .out1(regsel_R1), .out2(regsel_R2), .out3(regsel_R3), .sel(IR_L[6:5]));
  assign RegSel = and_1_out[3] ? {regsel_R3, regsel_R2, regsel_R1, regsel_R0} : 4'bz;  // Controlled_Buffer controlled_buffer_6
  assign FunSel = and_1_out[3] ? 2'b01 : 2'bz;  // Controlled_Buffer controlled_buffer_7
endmodule

module proj3_controlUnit_BRA (
  input  [7:0] Counter,
  input  isEnabled,
  output CounterReset,
  output [1:0] MuxBSel,
  output [2:0] ARegSel,
  output [1:0] AFunSel,
  output IR_selH
);

  wire [7:0] and_1_out, bit_extender_1_out;

  assign bit_extender_1_out = {{7{isEnabled}}, isEnabled};  // Bit_Extender bit_extender_1
  assign and_1_out = Counter & bit_extender_1_out;  // AND_Gate and_1, 8 bits wide
  assign IR_selH = and_1_out[2] ? 1'b0 : 1'bz;  // Controlled_Buffer controlled_buffer_1
  assign MuxBSel = and_1_out[2] ? 2'b01 : 2'bz;  // Controlled_Buffer controlled_buffer_2
  assign CounterReset = and_1_out[3] ? 1'b1 : 1'bz;  // Controlled_Buffer controlled_buffer_3
  assign ARegSel = and_1_out[2] ? 3'b001 : 3'bz;  // Controlled_Buffer controlled_buffer_4
  assign AFunSel = and_1_out[2] ? 2'b01 : 2'bz;  // Controlled_Buffer controlled_buffer_5
endmodule

module proj3_controlUnit_BEQ (
  input  Z,
  input  [7:0] Counter,
  input  isEnabled,
  output [1:0] MuxBSel,
  output [2:0] ARegSel,
  output [1:0] AFunSel,
  output IR_selH,
  output CounterReset
);

  wire and_2_out;
  wire [7:0] and_1_out, bit_extender_1_out;

  assign bit_extender_1_out = {{7{isEnabled}}, isEnabled};  // Bit_Extender bit_extender_1
  assign and_1_out = Counter & bit_extender_1_out;  // AND_Gate and_1, 8 bits wide
  and and_2 (and_2_out, Z, and_1_out[2]);
  assign CounterReset = and_1_out[3] ? 1'b1 : 1'bz;  // Controlled_Buffer controlled_buffer_1
  proj3_controlUnit_BRA proj3_controlunit_bra_1 (
    .ARegSel(ARegSel), .MuxBSel(MuxBSel), .AFunSel(AFunSel), .IR_selH(IR_selH), .isEnabled(and_2_out),
    .Counter(Counter));  // open: CounterReset
endmodule

module proj3_controlUnit_BNE (
  input  Z,
  input  [7:0] Counter,
  input  isEnabled,
  output [1:0] MuxBSel,
  output [2:0] ARegSel,
  output [1:0] AFunSel,
  output IR_selH,
  output CounterReset
);

  wire and_2_out;
  wire [7:0] and_1_out, bit_extender_1_out;

  assign bit_extender_1_out = {{7{isEnabled}}, isEnabled};  // Bit_Extender bit_extender_1
  assign and_1_out = Counter & bit_extender_1_out;  // AND_Gate and_1, 8 bits wide
  and and_2 (and_2_out, ~Z, and_1_out[2]);  // AND_Gate
  assign CounterReset = and_1_out[3] ? 1'b1 : 1'bz;  // Controlled_Buffer controlled_buffer_1
  proj3_controlUnit_BRA proj3_controlunit_bra_1 (
    .ARegSel(ARegSel), .MuxBSel(MuxBSel), .AFunSel(AFunSel), .IR_selH(IR_selH), .isEnabled(and_2_out),
    .Counter(Counter));  // open: CounterReset
endmodule

module proj3_controlUnit_CALL (
  input  [7:0] Counter,
  input  isEnabled,
  output [1:0] OutDSel,
  output [1:0] OutCSel,
  output CounterReset,
  output [1:0] MuxASel,
  output [3:0] FunSelAlu,
  output [1:0] MuxBSel,
  output [2:0] ARegSel,
  output [1:0] AFunSel,
  output MuxCSel,
  output RAM_WriteEnable,
  output IR_selH
);

  wire [7:0] and_1_out, bit_extender_1_out;

  assign bit_extender_1_out = {{7{isEnabled}}, isEnabled};  // Bit_Extender bit_extender_1
  assign and_1_out = Counter & bit_extender_1_out;  // AND_Gate and_1, 8 bits wide
  assign OutDSel = and_1_out[2] ? 2'b10 : 2'bz;  // Controlled_Buffer controlled_buffer_1
  assign OutCSel = and_1_out[2] ? 2'b00 : 2'bz;  // Controlled_Buffer controlled_buffer_2
  assign MuxASel = and_1_out[2] ? 2'b10 : 2'bz;  // Controlled_Buffer controlled_buffer_3
  assign ARegSel = and_1_out[3] ? 3'b001 : 3'bz;  // Controlled_Buffer controlled_buffer_4
  assign CounterReset = and_1_out[4] ? 1'b1 : 1'bz;  // Controlled_Buffer controlled_buffer_5
  assign MuxCSel = and_1_out[2] ? 1'b0 : 1'bz;  // Controlled_Buffer controlled_buffer_6
  assign AFunSel = and_1_out[3] ? 2'b01 : 2'bz;  // Controlled_Buffer controlled_buffer_7
  assign FunSelAlu = and_1_out[2] ? 4'b0000 : 4'bz;  // Controlled_Buffer controlled_buffer_8
  assign IR_selH = and_1_out[3] ? 1'b0 : 1'bz;  // Controlled_Buffer controlled_buffer_9
  assign RAM_WriteEnable = and_1_out[2] ? 1'b1 : 1'bz;  // Controlled_Buffer controlled_buffer_10
  assign MuxBSel = and_1_out[3] ? 2'b01 : 2'bz;  // Controlled_Buffer controlled_buffer_11
  assign ARegSel = and_1_out[2] ? 3'b100 : 3'bz;  // Controlled_Buffer controlled_buffer_12
  assign AFunSel = and_1_out[2] ? 2'b11 : 2'bz;  // Controlled_Buffer controlled_buffer_13
endmodule

module proj3_controlUnit_RET (
  input  [7:0] Counter,
  input  isEnabled,
  output CounterReset,
  output [1:0] OutDSel,
  output [1:0] MuxBSel,
  output [2:0] ARegSel,
  output [1:0] AFunSel
);

  wire [7:0] and_1_out, bit_extender_1_out;

  assign bit_extender_1_out = {{7{isEnabled}}, isEnabled};  // Bit_Extender bit_extender_1
  assign and_1_out = Counter & bit_extender_1_out;  // AND_Gate and_1, 8 bits wide
  assign ARegSel = and_1_out[2] ? 3'b100 : 3'bz;  // Controlled_Buffer controlled_buffer_1
  assign MuxBSel = and_1_out[3] ? 2'b10 : 2'bz;  // Controlled_Buffer controlled_buffer_2
  assign CounterReset = and_1_out[4] ? 1'b1 : 1'bz;  // Controlled_Buffer controlled_buffer_3
  assign AFunSel = and_1_out[2] ? 2'b10 : 2'bz;  // Controlled_Buffer controlled_buffer_4
  assign ARegSel = and_1_out[3] ? 3'b001 : 3'bz;  // Controlled_Buffer controlled_buffer_5
  assign AFunSel = and_1_out[3] ? 2'b01 : 2'bz;  // Controlled_Buffer controlled_buffer_6
  assign OutDSel = and_1_out[3] ? 2'b10 : 2'bz;  // Controlled_Buffer controlled_buffer_7
endmodule

module proj3_controlUnit_INCDEC (
  input  [7:0] Counter,
  input  isEnabled,
  input  [7:0] IR_L,
  input  [7:0] IR_H,
  output [1:0] OutCSel,
  output [1:0] MuxASel,
  output [3:0] FunSelAlu,
  output [1:0] MuxBSel,
  output MuxCSel,
  output [1:0] OutBSel,
  output CounterReset,
  output [3:0] RegSel,
  output [1:0] FunSel,
  output [2:0] ARegSel,
  output [1:0] AFunSel
);

  wire and_2_out, and_3_out, decoder_1_out4, decoder_1_out5, movEnabled, or_1_out, or_2_out,
       proj3_controlunit_mov_1_counterreset, srcreg1_AR, srcreg1_PC, srcreg1_R0, srcreg1_R1, srcreg1_R2,
       srcreg1_R3, srcreg1_SP;
  wire [1:0] operation;
  wire [4:0] fakeSrc;
  wire [7:0] and_1_out, bit_extender_1_out, mov_IR_H, mov_IR_L, movCounter, shifter_1_out, shifter_2_out;

  assign bit_extender_1_out = {{7{isEnabled}}, isEnabled};  // Bit_Extender bit_extender_1
  assign and_1_out = Counter & bit_extender_1_out;  // AND_Gate and_1, 8 bits wide
  assign mov_IR_H = and_1_out[3] ? IR_H : 8'bz;  // Controlled_Buffer controlled_buffer_1
  and and_2 (and_2_out, or_1_out, and_1_out[2]);
  or or_1 (or_1_out, srcreg1_PC, srcreg1_AR, srcreg1_SP);
  assign mov_IR_H = and_1_out[4] ? IR_H : 8'bz;  // Controlled_Buffer controlled_buffer_2
  assign movEnabled = and_1_out[3] ? 1'b1 : 1'bz;  // Controlled_Buffer controlled_buffer_3
  assign movEnabled = and_1_out[4] ? 1'b1 : 1'bz;  // Controlled_Buffer controlled_buffer_4
  assign ARegSel = and_2_out ? {srcreg1_SP, srcreg1_AR, srcreg1_PC} : 3'bz;  // Controlled_Buffer controlled_buffer_5
  Shifter #(.shift("lr")) shifter_1 (.in(Counter), .\dist (3'b001), .out(shifter_1_out));
  Shifter #(.shift("lr")) shifter_2 (.in(Counter), .\dist (3'b010), .out(shifter_2_out));
  assign AFunSel = and_2_out ? operation : 2'bz;  // Controlled_Buffer controlled_buffer_6
  assign movCounter = and_1_out[3] ? shifter_1_out : 8'bz;  // Controlled_Buffer controlled_buffer_7
  assign movCounter = and_1_out[4] ? shifter_2_out : 8'bz;  // Controlled_Buffer controlled_buffer_8
  Multiplexer #(.enable("false"), .width(2)) multiplexer_1 (.in0(2'b10), .in1(2'b11), .out(operation), .sel(IR_H[3]));
  or or_2 (or_2_out, srcreg1_R0, srcreg1_R1, srcreg1_R3, srcreg1_R2);
  and and_3 (and_3_out, and_1_out[2], or_2_out);
  assign mov_IR_L = and_1_out[3] ? IR_L : 8'bz;  // Controlled_Buffer controlled_buffer_9
  assign mov_IR_L = and_1_out[4] ? {IR_H[2:0], fakeSrc} : 8'bz;  // Controlled_Buffer controlled_buffer_10
  assign CounterReset = and_1_out[5] ? 1'b1 : 1'bz;  // Controlled_Buffer controlled_buffer_11
  assign RegSel = and_3_out ? {srcreg1_R3, srcreg1_R2, srcreg1_R1, srcreg1_R0} : 4'bz;  // Controlled_Buffer controlled_buffer_12
  assign FunSel = and_3_out ? operation : 2'bz;  // Controlled_Buffer controlled_buffer_13
  Decoder #(.enable("false"), .select(3)) decoder_1 (
    .out0(srcreg1_R0), .out1(srcreg1_R1), .out2(srcreg1_R2), .out3(srcreg1_R3), .out4(decoder_1_out4),
    .out5(decoder_1_out5), .out6(srcreg1_AR), .out7(srcreg1_SP), .sel(IR_L[7:5]));
  proj3_controlUnit_MOV proj3_controlunit_mov_1 (
    .FunSel(FunSel), .RegSel(RegSel), .OutCSel(OutCSel), .MuxASel(MuxASel), .FunSelAlu(FunSelAlu),
    .MuxBSel(MuxBSel), .ARegSel(ARegSel), .AFunSel(AFunSel), .OutBSel(OutBSel), .MuxCSel(MuxCSel),
    .CounterReset(proj3_controlunit_mov_1_counterreset), .IR_L(mov_IR_L), .isEnabled(movEnabled),
    .Counter(movCounter), .IR_H(mov_IR_H));
  or or_3 (srcreg1_PC, decoder_1_out4, decoder_1_out5);
  // also tied to GND on the sheet: proj3_controlunit_mov_1_counterreset

  // Other names for the same wires on the sheet: fakeSrc[7:5] = IR_H[2:0]; isDec = IR_H[3]
endmodule

module proj3_controlUnit_ALUOperations_alternative (
  input  [7:0] IR_H,
  input  [7:0] Counter,
  input  [7:0] IR_L,
  input  isEnabled,
  output [3:0] RegSel,
  output [1:0] FunSel,
  output [1:0] OutCSel,
  output [1:0] MuxASel,
  output [3:0] FunSelAlu,
  output [1:0] MuxBSel,
  output [2:0] ARegSel,
  output [1:0] AFunSel,
  output [1:0] OutASel,
  output [1:0] OutBSel,
  output MuxCSel,
  output CounterReset
);

  wire and_2_out, and_3_out, and_4_out, and_5_out, and_6_out, and_7_out, and_8_out, and_9_out, and_14_out,
       and_15_out, and_16_out, and_17_out, decoder_2_out4, decoder_2_out5, decoder_3_out4, decoder_3_out5,
       decoder_4_out4, decoder_4_out5, dstreg_AR, dstreg_PC, dstreg_R0, dstreg_R1, dstreg_R2, dstreg_R3,
       dstreg_SP, isSub, movEnabled, or_1_out, or_2_out, or_3_out, or_4_out, or_5_out, or_6_out,
       proj3_controlunit_mov_1_counterreset, src1_R0_R1_R2_R3, src2_R0_R1_R2_R3, srcreg1_AR, srcreg1_PC,
       srcreg1_R0, srcreg1_R1, srcreg1_R2, srcreg1_R3, srcreg1_SP, srcreg2_AR, srcreg2_PC, srcreg2_R0,
       srcreg2_R1, srcreg2_R2, srcreg2_R3, srcreg2_SP;
  wire [1:0] and_11_out, and_13_out, multiplexer_4_out, multiplexer_5_out;
  wire [2:0] mode;
  wire [3:0] multiplexer_1_out;
  wire [4:0] undriven, undriven_2;
  wire [7:0] and_1_out, bit_extender_1_out, mov_IR_H, mov_IR_L, movCounter, multiplexer_2_out,
       multiplexer_3_out, shifter_1_out;

  assign bit_extender_1_out = {{7{isEnabled}}, isEnabled};  // Bit_Extender bit_extender_1
  assign and_1_out = Counter & bit_extender_1_out;  // AND_Gate and_1, 8 bits wide
  assign CounterReset = and_1_out[5] ? 1'b1 : 1'bz;  // Controlled_Buffer controlled_buffer_1
  Multiplexer #(.enable("false"), .select(3), .width(4)) multiplexer_1 (
    .in0(4'b0100), .in1(4'b0110), .in2(4'b0111), .in3(4'b1000), .in4(4'b0010), .in5(4'b1010), .in6(4'b1011),
    .out(multiplexer_1_out), .sel(mode));  // open: in7
  and and_2 (and_2_out, or_1_out, and_1_out[2]);
  not not_1 (src1_R0_R1_R2_R3, or_1_out);
  or or_1 (or_1_out, srcreg1_PC, srcreg1_AR, srcreg1_SP);
  not not_2 (src2_R0_R1_R2_R3, or_2_out);
  assign FunSelAlu = and_1_out[4] ? multiplexer_1_out : 4'bz;  // Controlled_Buffer controlled_buffer_2
  Decoder #(.enable("false"), .select(3)) decoder_1 (
    .out1(isSub), .sel(mode));  // open: out0, out2, out3, out4, out5, out6, out7
  and and_3 (and_3_out, or_2_out, and_1_out[3]);
  or or_2 (or_2_out, srcreg2_PC, srcreg2_AR, srcreg2_SP);
  Multiplexer #(.enable("false"), .width(8)) multiplexer_2 (
    .in0(8'h2), .in1(8'h3), .out(multiplexer_2_out), .sel(srcreg1_R2));
  or or_3 (or_3_out, srcreg2_PC, srcreg2_AR, srcreg2_SP);
  Multiplexer #(.enable("false"), .width(8)) multiplexer_3 (
    .in0({8{1'b0}}), .in1(8'h1), .out(multiplexer_3_out), .sel(srcreg2_R0));
  assign mov_IR_H = and_3_out ? multiplexer_2_out : 8'bz;  // Controlled_Buffer controlled_buffer_3
  and and_4 (and_4_out, or_4_out, and_1_out[4]);
  or or_4 (or_4_out, dstreg_PC, dstreg_AR, dstreg_SP);
  and and_5 (and_5_out, or_3_out, and_1_out[4]);
  assign mov_IR_H = and_2_out ? multiplexer_3_out : 8'bz;  // Controlled_Buffer controlled_buffer_4
  assign MuxBSel = and_4_out ? 2'b11 : 2'bz;  // Controlled_Buffer controlled_buffer_5
  Multiplexer #(.enable("false"), .width(2)) multiplexer_4 (
    .in0(2'b10), .in1(2'b11), .out(multiplexer_4_out), .sel(srcreg1_R2));
  Demultiplexer #(.disabled("Z"), .tristate("true"), .width(2)) demultiplexer_1 (
    .out0(OutBSel), .out1(OutASel), .in(multiplexer_4_out), .sel(isSub), .en(and_5_out));
  assign movEnabled = and_2_out ? 1'b1 : 1'bz;  // Controlled_Buffer controlled_buffer_6
  assign movEnabled = and_3_out ? 1'b1 : 1'bz;  // Controlled_Buffer controlled_buffer_7
  assign ARegSel = and_4_out ? {dstreg_SP, dstreg_AR, dstreg_PC} : 3'bz;  // Controlled_Buffer controlled_buffer_8
  assign MuxCSel = and_1_out[4] ? 1'b1 : 1'bz;  // Controlled_Buffer controlled_buffer_9
  Shifter #(.shift("lr")) shifter_1 (.in(Counter), .\dist (3'b001), .out(shifter_1_out));
  assign AFunSel = and_4_out ? 2'b01 : 2'bz;  // Controlled_Buffer controlled_buffer_10
  and and_6 (and_6_out, or_5_out, and_1_out[4]);
  or or_5 (or_5_out, srcreg1_PC, srcreg1_AR, srcreg1_SP);
  assign movCounter = and_2_out ? Counter : 8'bz;  // Controlled_Buffer controlled_buffer_11
  assign movCounter = and_3_out ? shifter_1_out : 8'bz;  // Controlled_Buffer controlled_buffer_12
  Multiplexer #(.enable("false"), .width(2)) multiplexer_5 (
    .in0(2'b00), .in1(2'b01), .out(multiplexer_5_out), .sel(srcreg2_R0));
  and and_7 (and_7_out, and_1_out[4], or_6_out);
  or or_6 (or_6_out, dstreg_R0, dstreg_R1, dstreg_R3, dstreg_R2);
  Demultiplexer #(.disabled("Z"), .tristate("true"), .width(2)) demultiplexer_2 (
    .out0(OutASel), .out1(OutBSel), .in(multiplexer_5_out), .sel(isSub), .en(and_6_out));
  and and_8 (and_8_out, src1_R0_R1_R2_R3, and_1_out[4]);
  assign MuxASel = and_7_out ? 2'b11 : 2'bz;  // Controlled_Buffer controlled_buffer_13
  and and_9 (and_9_out, src2_R0_R1_R2_R3, and_1_out[4]);
  assign mov_IR_L = and_2_out ? {IR_L[7:5], undriven_2} : 8'bz;  // Controlled_Buffer controlled_buffer_14
  assign mov_IR_L = and_3_out ? {IR_L[4:2], undriven} : 8'bz;  // Controlled_Buffer controlled_buffer_15
  and and_10 (and_11_out[1], ~srcreg2_R0, ~srcreg2_R1);  // AND_Gate
  and and_11 (and_11_out[0], ~srcreg2_R2, ~srcreg2_R0);  // AND_Gate
  assign RegSel = and_7_out ? {dstreg_R3, dstreg_R2, dstreg_R1, dstreg_R0} : 4'bz;  // Controlled_Buffer controlled_buffer_16
  Demultiplexer #(.disabled("Z"), .tristate("true"), .width(2)) demultiplexer_3 (
    .out0(OutBSel), .out1(OutASel), .in(and_11_out), .sel(isSub), .en(and_9_out));
  and and_12 (and_13_out[1], ~srcreg1_R0, ~srcreg1_R1);  // AND_Gate
  and and_13 (and_13_out[0], ~srcreg1_R2, ~srcreg1_R0);  // AND_Gate
  assign FunSel = and_7_out ? 2'b01 : 2'bz;  // Controlled_Buffer controlled_buffer_17
  Demultiplexer #(.disabled("Z"), .tristate("true"), .width(2)) demultiplexer_4 (
    .out0(OutASel), .out1(OutBSel), .in(and_13_out), .sel(isSub), .en(and_8_out));
  and and_14 (and_14_out, IR_H[6], IR_H[5]);
  and and_15 (and_15_out, IR_H[4], IR_H[3]);
  or or_7 (mode[2], and_14_out, and_15_out);
  not not_3 (mode[0], IR_H[3]);
  and and_16 (and_16_out, IR_H[6], ~IR_H[4], IR_H[3]);  // AND_Gate
  or or_8 (mode[1], and_16_out, and_17_out);
  proj3_controlUnit_MOV proj3_controlunit_mov_1 (
    .FunSel(FunSel), .RegSel(RegSel), .OutCSel(OutCSel), .MuxASel(MuxASel), .FunSelAlu(FunSelAlu),
    .MuxBSel(MuxBSel), .ARegSel(ARegSel), .AFunSel(AFunSel), .OutBSel(OutBSel), .MuxCSel(MuxCSel),
    .CounterReset(proj3_controlunit_mov_1_counterreset), .IR_L(mov_IR_L), .isEnabled(movEnabled),
    .Counter(movCounter), .IR_H(mov_IR_H));
  Decoder #(.enable("false"), .select(3)) decoder_2 (
    .out0(dstreg_R0), .out1(dstreg_R1), .out2(dstreg_R2), .out3(dstreg_R3), .out4(decoder_2_out4),
    .out5(decoder_2_out5), .out6(dstreg_AR), .out7(dstreg_SP), .sel(IR_H[2:0]));
  and and_17 (and_17_out, ~IR_H[5], ~IR_H[3]);  // AND_Gate
  Decoder #(.enable("false"), .select(3)) decoder_3 (
    .out0(srcreg1_R0), .out1(srcreg1_R1), .out2(srcreg1_R2), .out3(srcreg1_R3), .out4(decoder_3_out4),
    .out5(decoder_3_out5), .out6(srcreg1_AR), .out7(srcreg1_SP), .sel(IR_L[7:5]));
  or or_9 (srcreg1_PC, decoder_3_out4, decoder_3_out5);
  or or_10 (dstreg_PC, decoder_2_out4, decoder_2_out5);
  Decoder #(.enable("false"), .select(3)) decoder_4 (
    .out0(srcreg2_R0), .out1(srcreg2_R1), .out2(srcreg2_R2), .out3(srcreg2_R3), .out4(decoder_4_out4),
    .out5(decoder_4_out5), .out6(srcreg2_AR), .out7(srcreg2_SP), .sel(IR_L[4:2]));
  or or_11 (srcreg2_PC, decoder_4_out4, decoder_4_out5);
  // also tied to GND on the sheet: proj3_controlunit_mov_1_counterreset
endmodule

module proj3_controlUnit_INC_alternative (
  input  [2:0] in_1,
  input  [2:0] in_2,
  input  [7:0] Counter,
  input  IsEnabled,
  output [2:0] AR_RegSel,
  output [1:0] out_6,
  output [1:0] out_7,
  output [1:0] AR_FunSel,
  output [1:0] out_9,
  output out_10,
  output [1:0] out_11,
  output out_12,
  output out_13,
  output [1:0] out_14,
  output [1:0] out_15,
  output [1:0] out_16,
  output [3:0] GPR_RegSel,
  output [1:0] GPR_FunSel,
  output [3:0] ALU_FunSel,
  output Ram_Write,
  output out_21
);

  wire and_1_out, and_2_out, and_3_out, and_4_out, and_5_out, and_6_out, and_9_out, and_10_out, and_11_out,
       and_13_out, and_14_out, and_16_out, and_17_out, and_18_out, and_19_out, decoder_1_out4,
       decoder_1_out5, decoder_2_out4, decoder_2_out5, decoder_3_out4, decoder_3_out5, decoder_4_out4,
       decoder_4_out5, decoder_5_out4, decoder_5_out5, decoder_6_out4, decoder_6_out5, decoder_7_out4,
       decoder_7_out5, not_1_out, not_2_out, not_3_out, not_4_out, not_5_out, xor_1_out, xor_2_out, xor_3_out;
  wire [1:0] multiplexer_1_out, multiplexer_2_out, multiplexer_3_out, multiplexer_4_out, multiplexer_5_out;
  wire [2:0] or_1_out, or_2_out, or_3_out, or_4_out, or_5_out, or_6_out, or_7_out, xnor_1_out, xnor_2_out,
       xnor_3_out, xnor_4_out;
  wire [3:0] decoder_1_out0, decoder_2_out0, decoder_3_out0, decoder_4_out0, decoder_5_out0, decoder_6_out0;
  wire [7:0] and_7_out, and_8_out, and_12_out, and_15_out, bit_extender_1_out, bit_extender_2_out,
       bit_extender_3_out, bit_extender_4_out;

  and and_1 (and_1_out, IsEnabled, and_3_out);
  not not_1 (not_1_out, in_2[2]);
  and and_2 (and_2_out, IsEnabled, and_4_out);
  Bit_Extender #(.in_width(1), .out_width(8), .\type ("input")) bit_extender_1 (
    .in(and_1_out), .out(bit_extender_1_out));  // open: extend
  not not_2 (not_2_out, in_1[2]);
  and and_3 (and_3_out, not_1_out, not_2_out, not_3_out);
  assign bit_extender_2_out = {{7{and_2_out}}, and_2_out};  // Bit_Extender bit_extender_2
  xor xor_1 (xor_1_out, in_2[2], in_1[2]);
  and and_4 (and_4_out, xor_1_out, not_4_out);
  and and_5 (and_5_out, IsEnabled, and_9_out);
  and and_6 (and_6_out, IsEnabled, and_10_out);
  assign and_7_out = Counter & bit_extender_1_out;  // AND_Gate and_7, 8 bits wide
  not not_3 (not_3_out, and_11_out);
  assign and_8_out = Counter & bit_extender_2_out;  // AND_Gate and_8, 8 bits wide
  assign bit_extender_3_out = {{7{and_5_out}}, and_5_out};  // Bit_Extender bit_extender_3
  and and_9 (and_9_out, in_2[2], in_1[2], not_5_out);
  assign bit_extender_4_out = {{7{and_6_out}}, and_6_out};  // Bit_Extender bit_extender_4
  and and_10 (and_10_out, xnor_4_out[2], xnor_4_out[1], xnor_4_out[0]);
  assign xnor_1_out = ~(in_1 ^ in_2);  // XNOR_Gate xnor_1, 3 bits wide
  and and_11 (and_11_out, xnor_1_out[2], xnor_1_out[1], xnor_1_out[0]);
  assign xnor_2_out = ~(in_1 ^ in_2);  // XNOR_Gate xnor_2, 3 bits wide
  not not_4 (not_4_out, and_14_out);
  assign and_12_out = Counter & bit_extender_3_out;  // AND_Gate and_12, 8 bits wide
  not not_5 (not_5_out, and_13_out);
  and and_13 (and_13_out, xnor_3_out[2], xnor_3_out[1], xnor_3_out[0]);
  and and_14 (and_14_out, xnor_2_out[2], xnor_2_out[1], xnor_2_out[0]);
  assign xnor_3_out = ~(in_1 ^ in_2);  // XNOR_Gate xnor_3, 3 bits wide
  assign and_15_out = Counter & bit_extender_4_out;  // AND_Gate and_15, 8 bits wide
  assign GPR_RegSel = and_7_out[4] ? 4'b0000 : 4'bz;  // Controlled_Buffer controlled_buffer_1
  assign out_21 = and_7_out[5] ? 1'b1 : 1'bz;  // Controlled_Buffer controlled_buffer_2
  assign xnor_4_out = ~(in_1 ^ in_2);  // XNOR_Gate xnor_4, 3 bits wide
  assign out_15 = and_7_out[2] ? in_2[1:0] : 2'bz;  // Controlled_Buffer controlled_buffer_3
  assign GPR_RegSel = and_7_out[3] ? decoder_1_out0 : 4'bz;  // Controlled_Buffer controlled_buffer_4
  assign AR_RegSel = and_7_out[3] ? or_1_out : 3'bz;  // Controlled_Buffer controlled_buffer_5
  assign out_15 = and_8_out[2] ? in_2[1:0] : 2'bz;  // Controlled_Buffer controlled_buffer_6
  assign out_21 = and_8_out[5] ? 1'b1 : 1'bz;  // Controlled_Buffer controlled_buffer_7
  assign GPR_RegSel = and_8_out[3] ? decoder_2_out0 : 4'bz;  // Controlled_Buffer controlled_buffer_8
  assign AR_RegSel = and_8_out[3] ? or_2_out : 3'bz;  // Controlled_Buffer controlled_buffer_9
  assign GPR_RegSel = and_8_out[4] ? 4'b0000 : 4'bz;  // Controlled_Buffer controlled_buffer_10
  assign AR_RegSel = and_8_out[4] ? 3'b000 : 3'bz;  // Controlled_Buffer controlled_buffer_11
  assign GPR_RegSel = and_15_out[2] ? decoder_3_out0 : 4'bz;  // Controlled_Buffer controlled_buffer_12
  assign AR_RegSel = and_15_out[2] ? or_3_out : 3'bz;  // Controlled_Buffer controlled_buffer_13
  assign out_21 = and_15_out[3] ? 1'b1 : 1'bz;  // Controlled_Buffer controlled_buffer_14
  assign out_13 = and_7_out[2] ? 1'b1 : 1'bz;  // Controlled_Buffer controlled_buffer_15
  Decoder #(.enable("false"), .select(3)) decoder_1 (
    .out0(decoder_1_out0[0]), .out1(decoder_1_out0[1]), .out2(decoder_1_out0[2]), .out3(decoder_1_out0[3]),
    .out4(decoder_1_out4), .out5(decoder_1_out5), .out6(or_1_out[1]), .out7(or_1_out[2]), .sel(in_1));
  assign AR_RegSel = and_7_out[4] ? 3'b000 : 3'bz;  // Controlled_Buffer controlled_buffer_16
  assign out_13 = and_8_out[2] ? 1'b1 : 1'bz;  // Controlled_Buffer controlled_buffer_17
  assign out_6 = and_12_out[2] ? multiplexer_1_out : 2'bz;  // Controlled_Buffer controlled_buffer_18
  assign GPR_RegSel = and_12_out[3] ? decoder_4_out0 : 4'bz;  // Controlled_Buffer controlled_buffer_19
  assign out_21 = and_12_out[5] ? 1'b1 : 1'bz;  // Controlled_Buffer controlled_buffer_20
  or or_1 (or_1_out[0], decoder_1_out4, decoder_1_out5);
  Decoder #(.enable("false"), .select(3)) decoder_2 (
    .out0(decoder_2_out0[0]), .out1(decoder_2_out0[1]), .out2(decoder_2_out0[2]), .out3(decoder_2_out0[3]),
    .out4(decoder_2_out4), .out5(decoder_2_out5), .out6(or_2_out[1]), .out7(or_2_out[2]), .sel(in_1));
  assign AR_RegSel = and_12_out[3] ? or_4_out : 3'bz;  // Controlled_Buffer controlled_buffer_21
  assign GPR_RegSel = and_12_out[4] ? 4'b0000 : 4'bz;  // Controlled_Buffer controlled_buffer_22
  Decoder #(.enable("false"), .select(3)) decoder_3 (
    .out0(decoder_3_out0[0]), .out1(decoder_3_out0[1]), .out2(decoder_3_out0[2]), .out3(decoder_3_out0[3]),
    .out4(decoder_3_out4), .out5(decoder_3_out5), .out6(or_3_out[1]), .out7(or_3_out[2]), .sel(in_1));
  assign ALU_FunSel = and_7_out[2] ? 4'b0000 : 4'bz;  // Controlled_Buffer controlled_buffer_23
  assign GPR_FunSel = and_7_out[3] ? 2'b10 : 2'bz;  // Controlled_Buffer controlled_buffer_24
  assign ALU_FunSel = and_8_out[2] ? 4'b0000 : 4'bz;  // Controlled_Buffer controlled_buffer_25
  or or_2 (or_2_out[0], decoder_2_out4, decoder_2_out5);
  Multiplexer #(.enable("false"), .select(2), .width(2)) multiplexer_1 (
    .in0(2'b00), .in1(2'b11), .in2(2'b01), .in3(2'b10), .out(multiplexer_1_out), .sel(in_2[1:0]));
  assign AR_RegSel = and_12_out[4] ? 3'b000 : 3'bz;  // Controlled_Buffer controlled_buffer_26
  or or_3 (or_3_out[0], decoder_3_out4, decoder_3_out5);
  assign GPR_FunSel = and_8_out[3] ? 2'b10 : 2'bz;  // Controlled_Buffer controlled_buffer_27
  Decoder #(.enable("false"), .select(3)) decoder_4 (
    .out0(decoder_4_out0[0]), .out1(decoder_4_out0[1]), .out2(decoder_4_out0[2]), .out3(decoder_4_out0[3]),
    .out4(decoder_4_out4), .out5(decoder_4_out5), .out6(or_4_out[1]), .out7(or_4_out[2]), .sel(in_1));
  assign GPR_FunSel = and_15_out[2] ? 2'b10 : 2'bz;  // Controlled_Buffer controlled_buffer_28
  assign out_14 = and_7_out[2] ? 2'b11 : 2'bz;  // Controlled_Buffer controlled_buffer_29
  assign out_15 = and_7_out[4] ? in_1[1:0] : 2'bz;  // Controlled_Buffer controlled_buffer_30
  assign out_7 = and_8_out[2] ? 2'b11 : 2'bz;  // Controlled_Buffer controlled_buffer_31
  assign out_14 = and_12_out[2] ? 2'b10 : 2'bz;  // Controlled_Buffer controlled_buffer_32
  or or_4 (or_4_out[0], decoder_4_out4, decoder_4_out5);
  assign GPR_FunSel = and_7_out[2] ? 2'b01 : 2'bz;  // Controlled_Buffer controlled_buffer_33
  assign AR_FunSel = and_8_out[3] ? 2'b10 : 2'bz;  // Controlled_Buffer controlled_buffer_34
  and and_16 (and_16_out, and_8_out[4], in_1[2]);
  assign AR_FunSel = and_12_out[3] ? 2'b10 : 2'bz;  // Controlled_Buffer controlled_buffer_35
  assign AR_FunSel = and_15_out[2] ? 2'b10 : 2'bz;  // Controlled_Buffer controlled_buffer_36
  and and_17 (and_17_out, and_15_out[2], in_1[2]);
  assign out_13 = and_7_out[4] ? 1'b1 : 1'bz;  // Controlled_Buffer controlled_buffer_37
  assign GPR_FunSel = and_8_out[2] ? 2'b01 : 2'bz;  // Controlled_Buffer controlled_buffer_38
  and and_18 (and_18_out, and_8_out[4], in_1[2]);
  xor xor_2 (xor_2_out, and_8_out[4], and_16_out);
  assign out_13 = and_12_out[2] ? 1'b0 : 1'bz;  // Controlled_Buffer controlled_buffer_39
  xor xor_3 (xor_3_out, and_15_out[2], and_17_out);
  assign GPR_RegSel = and_7_out[2] ? decoder_5_out0 : 4'bz;  // Controlled_Buffer controlled_buffer_40
  assign AR_RegSel = and_7_out[2] ? or_5_out : 3'bz;  // Controlled_Buffer controlled_buffer_41
  and and_19 (and_19_out, and_15_out[2], in_1[2]);
  assign ALU_FunSel = and_7_out[4] ? 4'b0000 : 4'bz;  // Controlled_Buffer controlled_buffer_42
  assign AR_FunSel = and_8_out[2] ? 2'b01 : 2'bz;  // Controlled_Buffer controlled_buffer_43
  assign ALU_FunSel = and_12_out[2] ? 4'b0000 : 4'bz;  // Controlled_Buffer controlled_buffer_44
  assign out_6 = and_12_out[4] ? multiplexer_2_out : 2'bz;  // Controlled_Buffer controlled_buffer_45
  Decoder #(.enable("false"), .select(3)) decoder_5 (
    .out0(decoder_5_out0[0]), .out1(decoder_5_out0[1]), .out2(decoder_5_out0[2]), .out3(decoder_5_out0[3]),
    .out4(decoder_5_out4), .out5(decoder_5_out5), .out6(or_5_out[1]), .out7(or_5_out[2]), .sel(in_1));
  assign out_7 = and_12_out[2] ? 2'b11 : 2'bz;  // Controlled_Buffer controlled_buffer_46
  Multiplexer #(.enable("false"), .select(2), .width(2)) multiplexer_2 (
    .in0(2'b00), .in1(2'b11), .in2(2'b01), .in3(2'b10), .out(multiplexer_2_out), .sel(in_1[1:0]));
  or or_5 (or_5_out[0], decoder_5_out4, decoder_5_out5);
  assign GPR_RegSel = and_8_out[2] ? decoder_6_out0 : 4'bz;  // Controlled_Buffer controlled_buffer_47
  assign AR_RegSel = and_8_out[2] ? or_6_out : 3'bz;  // Controlled_Buffer controlled_buffer_48
  assign out_6 = and_18_out ? multiplexer_3_out : 2'bz;  // Controlled_Buffer controlled_buffer_49
  assign out_15 = xor_2_out ? in_1[1:0] : 2'bz;  // Controlled_Buffer controlled_buffer_50
  Multiplexer #(.enable("false"), .select(2), .width(2)) multiplexer_3 (
    .in0(2'b00), .in1(2'b11), .in2(2'b01), .in3(2'b10), .out(multiplexer_3_out), .sel(in_1[1:0]));
  assign AR_RegSel = and_12_out[2] ? or_7_out : 3'bz;  // Controlled_Buffer controlled_buffer_51
  assign out_14 = and_12_out[4] ? 2'b10 : 2'bz;  // Controlled_Buffer controlled_buffer_52
  assign out_6 = and_19_out ? multiplexer_4_out : 2'bz;  // Controlled_Buffer controlled_buffer_53
  assign out_15 = xor_3_out ? in_2[1:0] : 2'bz;  // Controlled_Buffer controlled_buffer_54
  Decoder #(.enable("false"), .select(3)) decoder_6 (
    .out0(decoder_6_out0[0]), .out1(decoder_6_out0[1]), .out2(decoder_6_out0[2]), .out3(decoder_6_out0[3]),
    .out4(decoder_6_out4), .out5(decoder_6_out5), .out6(or_6_out[1]), .out7(or_6_out[2]), .sel(in_1));
  assign out_14 = and_18_out ? 2'b10 : 2'bz;  // Controlled_Buffer controlled_buffer_55
  assign out_13 = xor_2_out ? 1'b1 : 1'bz;  // Controlled_Buffer controlled_buffer_56
  Decoder #(.enable("false"), .select(3)) decoder_7 (
    .out4(decoder_7_out4), .out5(decoder_7_out5), .out6(or_7_out[1]), .out7(or_7_out[2]), .sel(in_1));  // open: out0, out1, out2, out3
  assign out_13 = and_12_out[4] ? 1'b0 : 1'bz;  // Controlled_Buffer controlled_buffer_57
  or or_6 (or_6_out[0], decoder_6_out4, decoder_6_out5);
  Multiplexer #(.enable("false"), .select(2), .width(2)) multiplexer_4 (
    .in0(2'b00), .in1(2'b11), .in2(2'b01), .in3(2'b10), .out(multiplexer_4_out), .sel(in_1[1:0]));
  assign out_13 = xor_3_out ? 1'b1 : 1'bz;  // Controlled_Buffer controlled_buffer_58
  assign ALU_FunSel = xor_2_out ? 4'b0000 : 4'bz;  // Controlled_Buffer controlled_buffer_59
  or or_7 (or_7_out[0], decoder_7_out4, decoder_7_out5);
  assign ALU_FunSel = and_12_out[4] ? 4'b0000 : 4'bz;  // Controlled_Buffer controlled_buffer_60
  assign out_6 = and_8_out[2] ? multiplexer_5_out : 2'bz;  // Controlled_Buffer controlled_buffer_61
  assign out_13 = and_18_out ? 1'b0 : 1'bz;  // Controlled_Buffer controlled_buffer_62
  assign GPR_FunSel = and_12_out[2] ? 2'b01 : 2'bz;  // Controlled_Buffer controlled_buffer_63
  assign out_14 = and_19_out ? 2'b10 : 2'bz;  // Controlled_Buffer controlled_buffer_64
  assign ALU_FunSel = xor_3_out ? 4'b0000 : 4'bz;  // Controlled_Buffer controlled_buffer_65
  assign ALU_FunSel = and_18_out ? 4'b0000 : 4'bz;  // Controlled_Buffer controlled_buffer_66
  Multiplexer #(.enable("false"), .select(2), .width(2)) multiplexer_5 (
    .in0(2'b00), .in1(2'b11), .in2(2'b01), .in3(2'b10), .out(multiplexer_5_out), .sel(in_2[1:0]));
  assign out_13 = and_19_out ? 1'b0 : 1'bz;  // Controlled_Buffer controlled_buffer_67
  assign out_14 = and_8_out[2] ? 2'b10 : 2'bz;  // Controlled_Buffer controlled_buffer_68
  assign ALU_FunSel = and_19_out ? 4'b0000 : 4'bz;  // Controlled_Buffer controlled_buffer_69

  // Other names for the same wires on the sheet: AFunSel[1:0] = AR_FunSel; ARegSel[2:0] = AR_RegSel;
  //   CounterReset = out_21; DESTREG[2:0] = in_1; FunSel[1:0] = GPR_FunSel; FunSelAlu[3:0] = ALU_FunSel;
  //   IR_Enable = out_12; IR_FunSel[1:0] = out_11; IR_selH = out_10; MuxASel[1:0] = out_14; MuxBSel[1:0] = out_7;
  //   MuxCSel = out_13; OutASel[1:0] = out_15; OutBSel[1:0] = out_16; OutCSel[1:0] = out_6; OutDSel[1:0] = out_9;
  //   RAM_WriteEnable = Ram_Write; RegSel[3:0] = GPR_RegSel; SRCREG1[2:0] = in_2

  // Notes on the sheet:
  //   RF TO RF
  //   RF TO AR or AR TO RF
  //   AR TO AR
  //   DESTREG = SRCREG1
  //   INC
endmodule

module proj3_controlUnit_NOT_alternative (
  input  [2:0] DESTREG,
  input  [7:0] Counter,
  input  [2:0] SRCREG1,
  input  IsEnabled,
  output [2:0] AR_RegSel,
  output [1:0] out_6,
  output [1:0] out_7,
  output [1:0] AR_FunSel,
  output [1:0] out_9,
  output out_10,
  output [1:0] out_11,
  output out_12,
  output out_13,
  output [1:0] out_14,
  output [1:0] out_15,
  output [1:0] out_16,
  output [3:0] GPR_RegSel,
  output [1:0] GPR_FunSel,
  output [3:0] ALU_FunSel,
  output Ram_Write,
  output out_21
);

  wire and_1_out, and_2_out, and_3_out, and_4_out, and_5_out, and_6_out, and_7_out, and_8_out,
       decoder_1_out4, decoder_1_out5, decoder_2_out4, decoder_2_out5, decoder_3_out4, decoder_3_out5,
       decoder_4_out4, decoder_4_out5, not_1_out, not_2_out, not_3_out, not_4_out;
  wire [1:0] AOutCSel, multiplexer_1_out, multiplexer_2_out;
  wire [2:0] or_1_out, or_2_out, or_3_out, or_4_out;
  wire [3:0] decoder_1_out0, decoder_2_out0, decoder_3_out0, decoder_4_out0;
  wire [7:0] and_9_out, and_10_out, and_11_out, and_12_out, bit_extender_1_out, bit_extender_2_out,
       bit_extender_3_out, bit_extender_4_out;

  and and_1 (and_1_out, IsEnabled, and_5_out);
  and and_2 (and_2_out, IsEnabled, and_6_out);
  not not_1 (not_1_out, SRCREG1[2]);
  and and_3 (and_3_out, IsEnabled, and_7_out);
  not not_2 (not_2_out, SRCREG1[2]);
  and and_4 (and_4_out, IsEnabled, and_8_out);
  assign bit_extender_1_out = {{7{and_1_out}}, and_1_out};  // Bit_Extender bit_extender_1
  and and_5 (and_5_out, SRCREG1[2], DESTREG[2]);
  assign bit_extender_2_out = {{7{and_2_out}}, and_2_out};  // Bit_Extender bit_extender_2
  not not_3 (not_3_out, DESTREG[2]);
  and and_6 (and_6_out, not_1_out, not_3_out);
  assign bit_extender_3_out = {{7{and_3_out}}, and_3_out};  // Bit_Extender bit_extender_3
  and and_7 (and_7_out, not_2_out, DESTREG[2]);
  assign bit_extender_4_out = {{7{and_4_out}}, and_4_out};  // Bit_Extender bit_extender_4
  and and_8 (and_8_out, SRCREG1[2], not_4_out);
  assign and_9_out = Counter & bit_extender_1_out;  // AND_Gate and_9, 8 bits wide
  assign and_10_out = Counter & bit_extender_2_out;  // AND_Gate and_10, 8 bits wide
  assign and_11_out = Counter & bit_extender_3_out;  // AND_Gate and_11, 8 bits wide
  assign and_12_out = Counter & bit_extender_4_out;  // AND_Gate and_12, 8 bits wide
  not not_4 (not_4_out, DESTREG[2]);
  assign out_21 = and_9_out[3] ? 1'b1 : 1'bz;  // Controlled_Buffer controlled_buffer_1
  assign out_21 = and_11_out[3] ? 1'b1 : 1'bz;  // Controlled_Buffer controlled_buffer_2
  assign out_6 = and_12_out[2] ? multiplexer_2_out : 2'bz;  // Controlled_Buffer controlled_buffer_3
  assign out_21 = and_12_out[4] ? 1'b1 : 1'bz;  // Controlled_Buffer controlled_buffer_4
  assign AOutCSel = and_9_out[2] ? multiplexer_1_out : 2'bz;  // Controlled_Buffer controlled_buffer_5
  assign out_21 = and_10_out[3] ? 1'b1 : 1'bz;  // Controlled_Buffer controlled_buffer_6
  assign out_15 = and_11_out[2] ? SRCREG1[1:0] : 2'bz;  // Controlled_Buffer controlled_buffer_7
  Multiplexer #(.enable("false"), .select(2), .width(2)) multiplexer_1 (
    .in0(2'b00), .in1(2'b11), .in2(2'b01), .in3(2'b10), .out(multiplexer_1_out), .sel(SRCREG1[1:0]));
  assign out_15 = and_10_out[2] ? SRCREG1[1:0] : 2'bz;  // Controlled_Buffer controlled_buffer_8
  Multiplexer #(.enable("false"), .select(2), .width(2)) multiplexer_2 (
    .in0(2'b00), .in1(2'b11), .in2(2'b01), .in3(2'b10), .out(multiplexer_2_out), .sel(SRCREG1[1:0]));
  assign out_13 = and_11_out[2] ? 1'b1 : 1'bz;  // Controlled_Buffer controlled_buffer_9
  assign out_14 = and_12_out[2] ? 2'b10 : 2'bz;  // Controlled_Buffer controlled_buffer_10
  assign out_14 = and_9_out[2] ? 2'b10 : 2'bz;  // Controlled_Buffer controlled_buffer_11
  assign out_13 = and_10_out[2] ? 1'b1 : 1'bz;  // Controlled_Buffer controlled_buffer_12
  assign out_13 = and_12_out[2] ? 1'b0 : 1'bz;  // Controlled_Buffer controlled_buffer_13
  assign out_14 = and_12_out[3] ? 2'b11 : 2'bz;  // Controlled_Buffer controlled_buffer_14
  assign out_13 = and_9_out[2] ? 1'b0 : 1'bz;  // Controlled_Buffer controlled_buffer_15
  assign ALU_FunSel = and_10_out[2] ? 4'b0010 : 4'bz;  // Controlled_Buffer controlled_buffer_16
  assign ALU_FunSel = and_11_out[2] ? 4'b0010 : 4'bz;  // Controlled_Buffer controlled_buffer_17
  assign ALU_FunSel = and_12_out[2] ? 4'b0010 : 4'bz;  // Controlled_Buffer controlled_buffer_18
  assign GPR_FunSel = and_12_out[3] ? 2'b01 : 2'bz;  // Controlled_Buffer controlled_buffer_19
  assign ALU_FunSel = and_9_out[2] ? 4'b0010 : 4'bz;  // Controlled_Buffer controlled_buffer_20
  assign out_14 = and_10_out[2] ? 2'b11 : 2'bz;  // Controlled_Buffer controlled_buffer_21
  assign out_7 = and_11_out[2] ? 2'b11 : 2'bz;  // Controlled_Buffer controlled_buffer_22
  assign GPR_RegSel = and_12_out[3] ? decoder_1_out0 : 4'bz;  // Controlled_Buffer controlled_buffer_23
  assign AR_RegSel = and_12_out[3] ? or_1_out : 3'bz;  // Controlled_Buffer controlled_buffer_24
  assign out_7 = and_9_out[2] ? 2'b11 : 2'bz;  // Controlled_Buffer controlled_buffer_25
  assign GPR_FunSel = and_10_out[2] ? 2'b01 : 2'bz;  // Controlled_Buffer controlled_buffer_26
  assign AR_FunSel = and_11_out[2] ? 2'b01 : 2'bz;  // Controlled_Buffer controlled_buffer_27
  assign GPR_RegSel = and_10_out[2] ? decoder_2_out0 : 4'bz;  // Controlled_Buffer controlled_buffer_28
  assign AR_RegSel = and_10_out[2] ? or_2_out : 3'bz;  // Controlled_Buffer controlled_buffer_29
  assign GPR_RegSel = and_11_out[2] ? decoder_3_out0 : 4'bz;  // Controlled_Buffer controlled_buffer_30
  Decoder #(.enable("false"), .select(3)) decoder_1 (
    .out0(decoder_1_out0[0]), .out1(decoder_1_out0[1]), .out2(decoder_1_out0[2]), .out3(decoder_1_out0[3]),
    .out4(decoder_1_out4), .out5(decoder_1_out5), .out6(or_1_out[1]), .out7(or_1_out[2]), .sel(DESTREG));
  assign AR_FunSel = and_9_out[2] ? 2'b01 : 2'bz;  // Controlled_Buffer controlled_buffer_31
  assign AR_RegSel = and_11_out[2] ? or_3_out : 3'bz;  // Controlled_Buffer controlled_buffer_32
  or or_1 (or_1_out[0], decoder_1_out4, decoder_1_out5);
  Decoder #(.enable("false"), .select(3)) decoder_2 (
    .out0(decoder_2_out0[0]), .out1(decoder_2_out0[1]), .out2(decoder_2_out0[2]), .out3(decoder_2_out0[3]),
    .out4(decoder_2_out4), .out5(decoder_2_out5), .out6(or_2_out[1]), .out7(or_2_out[2]), .sel(DESTREG));
  Decoder #(.enable("false"), .select(3)) decoder_3 (
    .out0(decoder_3_out0[0]), .out1(decoder_3_out0[1]), .out2(decoder_3_out0[2]), .out3(decoder_3_out0[3]),
    .out4(decoder_3_out4), .out5(decoder_3_out5), .out6(or_3_out[1]), .out7(or_3_out[2]), .sel(DESTREG));
  assign GPR_RegSel = and_9_out[2] ? decoder_4_out0 : 4'bz;  // Controlled_Buffer controlled_buffer_33
  assign AR_RegSel = and_9_out[2] ? or_4_out : 3'bz;  // Controlled_Buffer controlled_buffer_34
  or or_2 (or_2_out[0], decoder_2_out4, decoder_2_out5);
  or or_3 (or_3_out[0], decoder_3_out4, decoder_3_out5);
  Decoder #(.enable("false"), .select(3)) decoder_4 (
    .out0(decoder_4_out0[0]), .out1(decoder_4_out0[1]), .out2(decoder_4_out0[2]), .out3(decoder_4_out0[3]),
    .out4(decoder_4_out4), .out5(decoder_4_out5), .out6(or_4_out[1]), .out7(or_4_out[2]), .sel(DESTREG));
  or or_4 (or_4_out[0], decoder_4_out4, decoder_4_out5);

  // Other names for the same wires on the sheet: AFunSel[1:0] = AR_FunSel; ARegSel[2:0] = AR_RegSel;
  //   CounterReset = out_21; FunSel[1:0] = GPR_FunSel; FunSelAlu[3:0] = ALU_FunSel; IR_Enable = out_12;
  //   IR_FunSel[1:0] = out_11; IR_selH = out_10; MuxASel[1:0] = out_14; MuxBSel[1:0] = out_7; MuxCSel = out_13;
  //   OutASel[1:0] = out_15; OutBSel[1:0] = out_16; OutCSel[1:0] = out_6; OutDSel[1:0] = out_9;
  //   RAM_WriteEnable = Ram_Write; RegSel[3:0] = GPR_RegSel

  // Notes on the sheet:
  //   AR TO RF
  //   AR TO AR
  //   RF TO AR
  //   NOT
  //   RF TO RF
endmodule

module proj3_controlUnit_ADD_alternative (
  input  [2:0] in_1,
  input  [2:0] in_2,
  input  [2:0] in_3,
  input  [7:0] Counter,
  input  isEnabled,
  output [1:0] out_6,
  output [1:0] out_7,
  output [3:0] out_8,
  output out_9,
  output [1:0] out_10,
  output [1:0] out_11,
  output [3:0] out_12,
  output [2:0] out_13,
  output [1:0] out_14,
  output [1:0] out_15,
  output [1:0] out_16,
  output out_17
);

  wire and_2_out, and_3_out, and_4_out, and_5_out, and_6_out, decoder_1_out4, decoder_1_out5, decoder_2_out4,
       decoder_2_out5, decoder_3_out4, decoder_3_out5, nor_1_out, xor_1_out;
  wire [2:0] or_1_out, or_2_out, or_3_out;
  wire [3:0] decoder_1_out0, decoder_2_out0, decoder_3_out0;
  wire [7:0] and_1_out, bit_extender_1_out;

  assign bit_extender_1_out = {{7{isEnabled}}, isEnabled};  // Bit_Extender bit_extender_1
  assign and_1_out = Counter & bit_extender_1_out;  // AND_Gate and_1, 8 bits wide
  assign out_17 = and_1_out[3] ? 1'b1 : 1'bz;  // Controlled_Buffer controlled_buffer_1
  Decoder #(.select(3)) decoder_1 (
    .out0(decoder_1_out0[0]), .out1(decoder_1_out0[1]), .out2(decoder_1_out0[2]), .out3(decoder_1_out0[3]),
    .out4(decoder_1_out4), .out5(decoder_1_out5), .out6(or_1_out[1]), .out7(or_1_out[2]), .sel(in_1),
    .en(and_3_out));
  assign out_14 = and_3_out ? 2'b01 : 2'bz;  // Controlled_Buffer controlled_buffer_2
  assign out_6 = and_3_out ? 2'b11 : 2'bz;  // Controlled_Buffer controlled_buffer_3
  assign out_12 = and_3_out ? decoder_1_out0 : 4'bz;  // Controlled_Buffer controlled_buffer_4
  or or_1 (or_1_out[0], decoder_1_out4, decoder_1_out5);
  and and_2 (and_2_out, in_3[2], xor_1_out);
  and and_3 (and_3_out, and_1_out[2], and_2_out);
  assign out_16 = and_3_out ? in_2[1:0] : 2'bz;  // Controlled_Buffer controlled_buffer_5
  assign out_6 = and_3_out ? 2'b10 : 2'bz;  // Controlled_Buffer controlled_buffer_6
  assign out_9 = and_3_out ? 1'b0 : 1'bz;  // Controlled_Buffer controlled_buffer_7
  assign out_11 = and_3_out ? in_3[1:0] : 2'bz;  // Controlled_Buffer controlled_buffer_8
  assign out_8 = and_3_out ? 4'b0111 : 4'bz;  // Controlled_Buffer controlled_buffer_9
  assign out_13 = and_3_out ? or_1_out : 3'bz;  // Controlled_Buffer controlled_buffer_10
  nor nor_1 (nor_1_out, in_2[2], in_3[2]);
  xor xor_1 (xor_1_out, in_2[2], in_3[2]);
  Decoder #(.select(3)) decoder_2 (
    .out0(decoder_2_out0[0]), .out1(decoder_2_out0[1]), .out2(decoder_2_out0[2]), .out3(decoder_2_out0[3]),
    .out4(decoder_2_out4), .out5(decoder_2_out5), .out6(or_2_out[1]), .out7(or_2_out[2]), .sel(in_1),
    .en(and_4_out));
  assign out_14 = and_4_out ? 2'b01 : 2'bz;  // Controlled_Buffer controlled_buffer_11
  assign out_6 = and_4_out ? 2'b11 : 2'bz;  // Controlled_Buffer controlled_buffer_12
  assign out_8 = and_4_out ? 4'b0111 : 4'bz;  // Controlled_Buffer controlled_buffer_13
  assign out_9 = and_4_out ? 1'b1 : 1'bz;  // Controlled_Buffer controlled_buffer_14
  assign out_10 = and_4_out ? in_3[1:0] : 2'bz;  // Controlled_Buffer controlled_buffer_15
  assign out_11 = and_4_out ? in_2[1:0] : 2'bz;  // Controlled_Buffer controlled_buffer_16
  and and_4 (and_4_out, nor_1_out, and_1_out[2]);
  and and_5 (and_5_out, xor_1_out, in_2[2]);
  and and_6 (and_6_out, and_1_out[2], and_5_out);
  assign out_12 = and_4_out ? decoder_2_out0 : 4'bz;  // Controlled_Buffer controlled_buffer_17
  assign out_16 = and_6_out ? in_3[1:0] : 2'bz;  // Controlled_Buffer controlled_buffer_18
  assign out_6 = and_6_out ? 2'b10 : 2'bz;  // Controlled_Buffer controlled_buffer_19
  assign out_9 = and_6_out ? 1'b0 : 1'bz;  // Controlled_Buffer controlled_buffer_20
  assign out_11 = and_6_out ? in_2[1:0] : 2'bz;  // Controlled_Buffer controlled_buffer_21
  assign out_8 = and_6_out ? 4'b0111 : 4'bz;  // Controlled_Buffer controlled_buffer_22
  Decoder #(.select(3)) decoder_3 (
    .out0(decoder_3_out0[0]), .out1(decoder_3_out0[1]), .out2(decoder_3_out0[2]), .out3(decoder_3_out0[3]),
    .out4(decoder_3_out4), .out5(decoder_3_out5), .out6(or_3_out[1]), .out7(or_3_out[2]), .sel(in_1),
    .en(and_6_out));
  assign out_14 = and_6_out ? 2'b01 : 2'bz;  // Controlled_Buffer controlled_buffer_23
  assign out_6 = and_6_out ? 2'b11 : 2'bz;  // Controlled_Buffer controlled_buffer_24
  or or_2 (or_2_out[0], decoder_2_out4, decoder_2_out5);
  assign out_12 = and_6_out ? decoder_3_out0 : 4'bz;  // Controlled_Buffer controlled_buffer_25
  or or_3 (or_3_out[0], decoder_3_out4, decoder_3_out5);
  assign out_13 = and_4_out ? or_2_out : 3'bz;  // Controlled_Buffer controlled_buffer_26
  assign out_13 = and_6_out ? or_3_out : 3'bz;  // Controlled_Buffer controlled_buffer_27

  assign out_7 = out_6;
  assign out_15 = out_14;

  // Other names for the same wires on the sheet: ARegSel[2:0] = out_13; CounterReset = out_17; DESTREG[2:0] = in_1;
  //   AFunSel[1:0] = out_14; FunSel[1:0] = out_14; FunSelAlu[3:0] = out_8; MuxASel[1:0] = out_6; MuxBSel[1:0] = out_6;
  //   MuxCSel = out_9; OutASel[1:0] = out_10; OutBSel[1:0] = out_11; OutCSel[1:0] = out_16; RegSel[3:0] = out_12;
  //   SRCREG1[2:0] = in_2; SRCREG2[2:0] = in_3

  // Notes on the sheet:
  //   REG1 = ADR
  //   REG2 = ADR
endmodule
module proj3_controlUnit_LSR_alternative (
  input  [2:0] in_1,
  input  [2:0] in_2,
  input  [7:0] Counter,
  input  IsEnabled,
  output [1:0] OutASel,
  output [3:0] FunSelAlu,
  output MuxCSel,
  output [1:0] MuxASel,
  output [1:0] FunSel,
  output [3:0] RegSel,
  output [1:0] MuxBSel,
  output [1:0] AFunSel,
  output [2:0] ARegSel,
  output [1:0] OutCSel,
  output out_15
);

  wire and_2_out, and_3_out, and_4_out, and_5_out, and_6_out, and_7_out, and_8_out, and_9_out, and_10_out,
       and_11_out, decoder_1_out1, decoder_1_out2, decoder_1_out3, decoder_2_out1, decoder_2_out2,
       decoder_2_out3, decoder_3_out4, decoder_3_out5, decoder_3_out6, decoder_3_out7, decoder_5_out4,
       decoder_5_out5, decoder_6_out4, decoder_6_out5, not_1_out, not_2_out, not_3_out, not_4_out, not_5_out;
  wire [1:0] or_3_out, or_4_out;
  wire [2:0] controlled_buffer_13_out, controlled_buffer_23_out, controlled_buffer_27_out, or_5_out, or_6_out;
  wire [3:0] decoder_3_out0, decoder_4_out0, decoder_5_out0, decoder_6_out0, decoder_7_out0;
  wire [7:0] and_1_out, bit_extender_1_out;

  assign bit_extender_1_out = {{7{IsEnabled}}, IsEnabled};  // Bit_Extender bit_extender_1
  assign and_1_out = Counter & bit_extender_1_out;  // AND_Gate and_1, 8 bits wide
  assign out_15 = and_1_out[4] ? 1'b1 : 1'bz;  // Controlled_Buffer controlled_buffer_1
  not not_1 (not_1_out, in_1[2]);
  not not_2 (not_2_out, in_2[2]);
  and and_2 (and_2_out, not_1_out, not_2_out);
  and and_3 (and_3_out, and_2_out, and_1_out[2]);
  not not_3 (not_3_out, in_1[2]);
  and and_4 (and_4_out, not_3_out, in_2[2]);
  and and_5 (and_5_out, and_4_out, and_1_out[2]);
  and and_6 (and_6_out, in_1[2], not_4_out);
  and and_7 (and_7_out, and_6_out, and_1_out[2]);
  and and_8 (and_8_out, in_1[2], in_2[2]);
  and and_9 (and_9_out, and_8_out, and_1_out[2]);
  assign OutASel = and_3_out ? in_1[1:0] : 2'bz;  // Controlled_Buffer controlled_buffer_2
  not not_4 (not_4_out, in_2[2]);
  assign MuxCSel = and_5_out ? 1'b1 : 1'bz;  // Controlled_Buffer controlled_buffer_3
  Decoder #(.enable("false"), .select(2)) decoder_1 (
    .out1(decoder_1_out1), .out2(decoder_1_out2), .out3(decoder_1_out3), .sel(in_1[1:0]));  // open: out0
  or or_1 (or_3_out[1], decoder_1_out3, decoder_1_out1);
  assign OutCSel = and_7_out ? or_3_out : 2'bz;  // Controlled_Buffer controlled_buffer_4
  Decoder #(.enable("false"), .select(2)) decoder_2 (
    .out1(decoder_2_out1), .out2(decoder_2_out2), .out3(decoder_2_out3), .sel(in_1[1:0]));  // open: out0
  or or_2 (or_4_out[1], decoder_2_out3, decoder_2_out1);
  assign OutCSel = and_9_out ? or_4_out : 2'bz;  // Controlled_Buffer controlled_buffer_5
  assign FunSelAlu = and_3_out ? 4'b1011 : 4'bz;  // Controlled_Buffer controlled_buffer_6
  assign OutASel = and_5_out ? in_1[1:0] : 2'bz;  // Controlled_Buffer controlled_buffer_7
  or or_3 (or_3_out[0], decoder_1_out1, decoder_1_out2);
  assign MuxASel = and_7_out ? 2'b10 : 2'bz;  // Controlled_Buffer controlled_buffer_8
  or or_4 (or_4_out[0], decoder_2_out1, decoder_2_out2);
  assign MuxCSel = and_3_out ? 1'b1 : 1'bz;  // Controlled_Buffer controlled_buffer_9
  assign MuxASel = and_9_out ? 2'b10 : 2'bz;  // Controlled_Buffer controlled_buffer_10
  assign MuxASel = and_3_out ? 2'b11 : 2'bz;  // Controlled_Buffer controlled_buffer_11
  assign FunSelAlu = and_5_out ? 4'b1011 : 4'bz;  // Controlled_Buffer controlled_buffer_12
  assign controlled_buffer_13_out = and_7_out ? in_2 : 3'bz;  // Controlled_Buffer controlled_buffer_13
  Decoder #(.select(3)) decoder_3 (
    .out0(decoder_3_out0[0]), .out1(decoder_3_out0[1]), .out2(decoder_3_out0[2]), .out3(decoder_3_out0[3]),
    .out4(decoder_3_out4), .out5(decoder_3_out5), .out6(decoder_3_out6), .out7(decoder_3_out7),
    .sel(controlled_buffer_13_out), .en(and_7_out));
  assign MuxCSel = and_9_out ? 1'b0 : 1'bz;  // Controlled_Buffer controlled_buffer_14
  assign MuxBSel = and_5_out ? 2'b11 : 2'bz;  // Controlled_Buffer controlled_buffer_15
  assign RegSel = and_7_out ? decoder_3_out0 : 4'bz;  // Controlled_Buffer controlled_buffer_16
  assign FunSelAlu = and_9_out ? 4'b1011 : 4'bz;  // Controlled_Buffer controlled_buffer_17
  assign FunSel = and_3_out ? 2'b01 : 2'bz;  // Controlled_Buffer controlled_buffer_18
  assign FunSel = and_7_out ? 2'b01 : 2'bz;  // Controlled_Buffer controlled_buffer_19
  Decoder #(.enable("false"), .select(2)) decoder_4 (
    .out0(decoder_4_out0[0]), .out1(decoder_4_out0[1]), .out2(decoder_4_out0[2]), .out3(decoder_4_out0[3]),
    .sel(in_2[1:0]));
  assign AFunSel = and_5_out ? 2'b01 : 2'bz;  // Controlled_Buffer controlled_buffer_20
  assign MuxBSel = and_9_out ? 2'b11 : 2'bz;  // Controlled_Buffer controlled_buffer_21
  assign RegSel = and_3_out ? decoder_4_out0 : 4'bz;  // Controlled_Buffer controlled_buffer_22
  assign controlled_buffer_23_out = and_5_out ? in_2 : 3'bz;  // Controlled_Buffer controlled_buffer_23
  Decoder #(.select(3)) decoder_5 (
    .out0(decoder_5_out0[0]), .out1(decoder_5_out0[1]), .out2(decoder_5_out0[2]), .out3(decoder_5_out0[3]),
    .out4(decoder_5_out4), .out5(decoder_5_out5), .out6(or_5_out[1]), .out7(or_5_out[2]),
    .sel(controlled_buffer_23_out), .en(and_5_out));
  assign AFunSel = and_9_out ? 2'b01 : 2'bz;  // Controlled_Buffer controlled_buffer_24
  assign RegSel = and_5_out ? decoder_5_out0 : 4'bz;  // Controlled_Buffer controlled_buffer_25
  not not_5 (not_5_out, in_2[2]);
  and and_10 (and_10_out, in_1[2], not_5_out);
  and and_11 (and_11_out, and_10_out, and_1_out[3]);
  assign ARegSel = and_5_out ? or_5_out : 3'bz;  // Controlled_Buffer controlled_buffer_26
  or or_5 (or_5_out[0], decoder_5_out4, decoder_5_out5);
  assign controlled_buffer_27_out = and_9_out ? in_2 : 3'bz;  // Controlled_Buffer controlled_buffer_27
  Decoder #(.select(3)) decoder_6 (
    .out0(decoder_6_out0[0]), .out1(decoder_6_out0[1]), .out2(decoder_6_out0[2]), .out3(decoder_6_out0[3]),
    .out4(decoder_6_out4), .out5(decoder_6_out5), .out6(or_6_out[1]), .out7(or_6_out[2]),
    .sel(controlled_buffer_27_out), .en(and_9_out));
  assign MuxCSel = and_11_out ? 1'b1 : 1'bz;  // Controlled_Buffer controlled_buffer_28
  assign RegSel = and_9_out ? decoder_6_out0 : 4'bz;  // Controlled_Buffer controlled_buffer_29
  or or_6 (or_6_out[0], decoder_6_out4, decoder_6_out5);
  assign OutASel = and_11_out ? in_2[1:0] : 2'bz;  // Controlled_Buffer controlled_buffer_30
  assign FunSelAlu = and_11_out ? 4'b1011 : 4'bz;  // Controlled_Buffer controlled_buffer_31
  assign ARegSel = and_9_out ? or_6_out : 3'bz;  // Controlled_Buffer controlled_buffer_32
  assign MuxASel = and_11_out ? 2'b11 : 2'bz;  // Controlled_Buffer controlled_buffer_33
  assign FunSel = and_11_out ? 2'b01 : 2'bz;  // Controlled_Buffer controlled_buffer_34
  Decoder #(.enable("false"), .select(2)) decoder_7 (
    .out0(decoder_7_out0[0]), .out1(decoder_7_out0[1]), .out2(decoder_7_out0[2]), .out3(decoder_7_out0[3]),
    .sel(in_2[1:0]));
  assign RegSel = and_11_out ? decoder_7_out0 : 4'bz;  // Controlled_Buffer controlled_buffer_35

  // Other names for the same wires on the sheet: CounterReset = out_15; DESTREG[2:0] = in_2; SRCREG1[2:0] = in_1

  // Notes on the sheet:
  //   RF TO RF
  //   RF TO AR
  //   AR TO RF
  //   AR TO AR
endmodule
